// Logisim project AP1.circ as structural Verilog
module main (
  input  A,
  input  B,
  input  C,
  input  D,
  input  E,
  input  F,
  output out_7
);

  wire AD_out, BE_out, CF_out, not_1_out, not_2_out, not_3_out;

  xor AD (AD_out, A, D);
  not not_1 (not_1_out, AD_out);
  xor BE (BE_out, B, E);
  not not_2 (not_2_out, BE_out);
  xor CF (CF_out, C, F);
  not not_3 (not_3_out, CF_out);
  Ap1 ap1_1 ();  // open: clock, val, A, B, C, D, E, F, AD, BE, CF, max, cpt, H, I, J, G
  and G (out_7, not_1_out, not_3_out, not_2_out);
endmodule

// VHDL entity Ap1, as the project stores it:
--------------------------------------------------------------------------------
-- Project :
-- File    :
-- Autor   :
-- Date    :
--
--------------------------------------------------------------------------------
-- Description :
--
--------------------------------------------------------------------------------

LIBRARY ieee;
USE ieee.std_logic_1164.all;

ENTITY Ap1 IS
  PORT (
  ------------------------------------------------------------------------------
  --Insert input ports below
    clock      : IN  std_logic;                    -- input bit example
    val        : IN  std_logic_vector(3 DOWNTO 0); -- input vector example
    A          : IN  std_logic;
    B          : IN  std_logic;
    C          : IN  std_logic;
    D          : IN  std_logic;
    E          : IN  std_logic;
    F          : IN  std_logic;
    AD         : IN  std_logic;
    BE         : IN  std_logic;
    CF         : IN  std_logic;
  ------------------------------------------------------------------------------
  --Insert output ports below
    max        : OUT std_logic;                    -- output bit example
    cpt        : OUT std_logic_vector(3 DOWNTO 0);  -- output vector example
    H          : OUT std_logic;
    I          : OUT std_logic;
    J          : OUT std_logic;
    G          : OUT std_logic
    );
END Ap1;

--------------------------------------------------------------------------------
--Complete your VHDL description below
--------------------------------------------------------------------------------

ARCHITECTURE TypeArchitecture OF Ap1 IS

BEGIN

H <= A xnor D;
I <= B xnor E;
J <= C xnor F;
G <= AD and BE and CF;

END TypeArchitecture;
