// Logisim project AP2.circ as structural Verilog
module main (
  input  RBO2,
  input  LT,
  input  RBI,
  input  in_4,
  input  in_5,
  input  in_6,
  input  in_7,
  input  in_8,
  input  in_9,
  input  in_10,
  input  in_11
);

  wire and_1_out, and_2_out, and_3_out, and_4_out, and_5_out, and_6_out, and_7_out, and_8_out, and_9_out,
       and_10_out, and_11_out, and_12_out, and_13_out, and_14_out, and_15_out, and_16_out, and_17_out,
       and_18_out, and_19_out, and_20_out, and_21_out, and_22_out, and_23_out, and_24_out, and_25_out,
       and_26_out, and_27_out, and_28_out, and_29_out, and_30_out, and_31_out, and_32_out, and_33_out,
       and_34_out, and_35_out, and_36_out, and_37_out, and_38_out, and_39_out, and_40_out, and_41_out,
       and_42_out, and_43_out, and_44_out, and_45_out, and_46_out, and_47_out, and_48_out, and_49_out,
       and_50_out, and_51_out, and_52_out, and_53_out, and_54_out, and_55_out, and_56_out, and_57_out,
       and_58_out, and_59_out, and_60_out, e_out, f_out, g_out, nand_1_out, nand_2_out, nand_3_out,
       nand_4_out, nand_5_out, nand_6_out, nand_7_out, nand_8_out, not_1_out, not_2_out, or_1_out, or_2_out,
       or_3_out, or_4_out, or_5_out, or_6_out, or_7_out, pa_out, pb_out, pc_out, pd_out;

  and and_1 (and_1_out, not_1_out, not_2_out);
  not not_1 (not_1_out, LT);
  not not_2 (not_2_out, RBI);
  nand nand_1 (nand_1_out, not_2_out, ~in_4);  // NAND_Gate
  nand nand_2 (nand_2_out, not_2_out, ~in_5);  // NAND_Gate
  nand nand_3 (nand_3_out, not_2_out, ~in_6);  // NAND_Gate
  nand nand_4 (nand_4_out, not_2_out, ~in_7);  // NAND_Gate
  and and_2 (and_2_out, nand_1_out, ~nand_2_out, ~nand_3_out);  // AND_Gate
  and and_3 (and_3_out, ~nand_1_out, nand_2_out, nand_4_out);  // AND_Gate
  and and_4 (and_4_out, ~nand_1_out, ~nand_2_out, nand_3_out);  // AND_Gate
  and and_5 (and_5_out, ~nand_1_out, ~nand_2_out, ~nand_4_out);  // AND_Gate
  and and_6 (and_6_out, ~nand_1_out, ~nand_3_out, ~nand_4_out);  // AND_Gate
  and and_7 (and_7_out, ~nand_1_out, ~nand_2_out, nand_4_out);  // AND_Gate
  and and_8 (and_8_out, ~nand_1_out, ~nand_2_out, nand_3_out);  // AND_Gate
  and and_9 (and_9_out, ~nand_1_out, nand_3_out, nand_4_out);  // AND_Gate
  and and_10 (and_10_out, nand_1_out, ~nand_2_out, ~nand_3_out);  // AND_Gate
  and and_11 (and_11_out, ~nand_1_out, ~nand_3_out);  // AND_Gate
  and and_12 (and_12_out, ~nand_1_out, nand_3_out, nand_4_out);  // AND_Gate
  and and_13 (and_13_out, ~nand_1_out, nand_2_out, nand_3_out);  // AND_Gate
  and and_14 (and_14_out, nand_1_out, ~nand_2_out, ~nand_3_out);  // AND_Gate
  and and_15 (and_15_out, ~nand_1_out, ~nand_2_out, nand_3_out);  // AND_Gate
  and and_16 (and_16_out, ~nand_1_out, nand_3_out, ~nand_4_out);  // AND_Gate
  and and_17 (and_17_out, ~nand_1_out, ~nand_2_out, ~nand_4_out);  // AND_Gate
  and and_18 (and_18_out, ~nand_1_out, nand_2_out, ~nand_3_out, nand_4_out);  // AND_Gate
  and and_19 (and_19_out, nand_1_out, ~nand_2_out, ~nand_3_out);  // AND_Gate
  and and_20 (and_20_out, ~nand_1_out, ~nand_2_out, ~nand_4_out);  // AND_Gate
  and and_21 (and_21_out, ~nand_1_out, nand_3_out, ~nand_4_out);  // AND_Gate
  and and_22 (and_22_out, nand_1_out, ~nand_2_out, ~nand_3_out, ~nand_4_out);  // AND_Gate
  and and_23 (and_23_out, ~nand_1_out, ~nand_3_out, ~nand_4_out);  // AND_Gate
  and and_24 (and_24_out, ~nand_1_out, nand_2_out, ~nand_4_out);  // AND_Gate
  and and_25 (and_25_out, ~nand_1_out, nand_2_out, ~nand_3_out);  // AND_Gate
  and and_26 (and_26_out, nand_1_out, ~nand_2_out, ~nand_3_out);  // AND_Gate
  and and_27 (and_27_out, ~nand_1_out, nand_2_out, ~nand_3_out);  // AND_Gate
  and and_28 (and_28_out, ~nand_1_out, ~nand_2_out, nand_3_out);  // AND_Gate
  and and_29 (and_29_out, ~nand_1_out, nand_3_out, ~nand_4_out);  // AND_Gate
  and and_30 (and_30_out, nand_1_out, ~nand_2_out, ~nand_3_out);  // AND_Gate
  or pa (pa_out, and_2_out, and_3_out, and_4_out, and_5_out);
  or pb (pb_out, and_6_out, and_7_out, and_8_out, and_9_out, and_10_out);
  or pc (pc_out, and_11_out, and_12_out, and_13_out, and_14_out);
  or pd (pd_out, and_15_out, and_16_out, and_17_out, and_18_out, and_19_out);
  or e (e_out, and_20_out, and_21_out, and_22_out);
  or f (f_out, and_23_out, and_24_out, and_25_out, and_26_out);
  or g (g_out, and_27_out, and_28_out, and_1_out, and_29_out, and_30_out);
  _7_Segment_Display u_7_segment_display_1 (
    .g(g_out), .f(f_out), .a(pa_out), .b(pb_out), .e(e_out), .d(pd_out), .c(pc_out));  // open: dp
  _7_Segment_Display u_7_segment_display_2 (
    .g(or_7_out), .f(or_6_out), .a(or_1_out), .b(or_2_out), .e(or_5_out), .d(or_4_out), .c(or_3_out));  // open: dp
  nand nand_5 (nand_5_out, and_60_out, ~in_8);  // NAND_Gate
  nand nand_6 (nand_6_out, and_60_out, ~in_9);  // NAND_Gate
  nand nand_7 (nand_7_out, and_60_out, ~in_10);  // NAND_Gate
  nand nand_8 (nand_8_out, and_60_out, ~in_11);  // NAND_Gate
  and and_31 (and_31_out, nand_5_out, ~nand_6_out, ~nand_7_out);  // AND_Gate
  and and_32 (and_32_out, ~nand_5_out, nand_6_out, nand_8_out);  // AND_Gate
  and and_33 (and_33_out, ~nand_5_out, ~nand_6_out, nand_7_out);  // AND_Gate
  and and_34 (and_34_out, ~nand_5_out, ~nand_6_out, ~nand_8_out);  // AND_Gate
  and and_35 (and_35_out, ~nand_5_out, ~nand_7_out, ~nand_8_out);  // AND_Gate
  and and_36 (and_36_out, ~nand_5_out, ~nand_6_out, nand_8_out);  // AND_Gate
  and and_37 (and_37_out, ~nand_5_out, ~nand_6_out, nand_7_out);  // AND_Gate
  and and_38 (and_38_out, ~nand_5_out, nand_7_out, nand_8_out);  // AND_Gate
  and and_39 (and_39_out, nand_5_out, ~nand_6_out, ~nand_7_out);  // AND_Gate
  and and_40 (and_40_out, ~nand_5_out, ~nand_7_out);  // AND_Gate
  and and_41 (and_41_out, ~nand_5_out, nand_7_out, nand_8_out);  // AND_Gate
  and and_42 (and_42_out, ~nand_5_out, nand_6_out, nand_7_out);  // AND_Gate
  and and_43 (and_43_out, nand_5_out, ~nand_6_out, ~nand_7_out);  // AND_Gate
  and and_44 (and_44_out, ~nand_5_out, ~nand_6_out, nand_7_out);  // AND_Gate
  and and_45 (and_45_out, ~nand_5_out, nand_7_out, ~nand_8_out);  // AND_Gate
  and and_46 (and_46_out, ~nand_5_out, ~nand_6_out, ~nand_8_out);  // AND_Gate
  and and_47 (and_47_out, ~nand_5_out, nand_6_out, ~nand_7_out, nand_8_out);  // AND_Gate
  and and_48 (and_48_out, nand_5_out, ~nand_6_out, ~nand_7_out);  // AND_Gate
  and and_49 (and_49_out, ~nand_5_out, ~nand_6_out, ~nand_8_out);  // AND_Gate
  and and_50 (and_50_out, ~nand_5_out, nand_7_out, ~nand_8_out);  // AND_Gate
  and and_51 (and_51_out, nand_5_out, ~nand_6_out, ~nand_7_out, ~nand_8_out);  // AND_Gate
  and and_52 (and_52_out, ~nand_5_out, ~nand_7_out, ~nand_8_out);  // AND_Gate
  and and_53 (and_53_out, ~nand_5_out, nand_6_out, ~nand_8_out);  // AND_Gate
  and and_54 (and_54_out, ~nand_5_out, nand_6_out, ~nand_7_out);  // AND_Gate
  and and_55 (and_55_out, nand_5_out, ~nand_6_out, ~nand_7_out);  // AND_Gate
  and and_56 (and_56_out, ~nand_5_out, nand_6_out, ~nand_7_out);  // AND_Gate
  and and_57 (and_57_out, ~nand_5_out, ~nand_6_out, nand_7_out);  // AND_Gate
  and and_58 (and_58_out, ~nand_5_out, nand_7_out, ~nand_8_out);  // AND_Gate
  and and_59 (and_59_out, nand_5_out, ~nand_6_out, ~nand_7_out);  // AND_Gate
  or or_1 (or_1_out, and_31_out, and_32_out, and_33_out, and_34_out);
  or or_2 (or_2_out, and_35_out, and_36_out, and_37_out, and_38_out, and_39_out);
  or or_3 (or_3_out, and_40_out, and_41_out, and_42_out, and_43_out);
  or or_4 (or_4_out, and_44_out, and_45_out, and_46_out, and_47_out, and_48_out);
  or or_5 (or_5_out, and_49_out, and_50_out, and_51_out);
  or or_6 (or_6_out, and_52_out, and_53_out, and_54_out, and_55_out);
  or or_7 (or_7_out, and_56_out, and_57_out, and_58_out, and_59_out);
  and and_60 (and_60_out, not_2_out, RBO2);
endmodule

// VHDL entity Ap2, as the project stores it:
--------------------------------------------------------------------------------
-- Project :
-- File    :
-- Autor   :
-- Date    :
--
--------------------------------------------------------------------------------
-- Description :
--
--------------------------------------------------------------------------------

LIBRARY ieee;
USE ieee.std_logic_1164.all;

ENTITY Ap2 IS
  PORT (
  ------------------------------------------------------------------------------
  --Insert input ports below
    D1         : IN  std_logic;
    C1         : IN  std_logic;
    B1         : IN  std_logic;
    A1         : IN  std_logic;
    LT         : IN  std_logic;
    RBO        : IN  std_logic;
    RBO2       : IN  std_logic;
    
    
  ------------------------------------------------------------------------------
  --Insert output ports below
    a          : OUT std_logic;
    b          : OUT std_logic;
    c          : OUT std_logic;
    d          : OUT std_logic;
    e          : OUT std_logic;
    f          : OUT std_logic;
    g          : OUT std_logic;
    RBI        : OUT std_logic
    
    
    );
END Ap2;

--------------------------------------------------------------------------------
--Complete your VHDL description below
--------------------------------------------------------------------------------

ARCHITECTURE TypeArchitecture OF Ap2 IS

BEGIN

a <= A1 and not B1 and  not C1;
a <= not A1 and B1 and  D1;
a <= not A1 and not B1 and  C1;
a <= not A1 and not B1 and  not D1;
b <= not A1 and not c1 and  not D1;
b <= not A1 and not C1 and  D1;
b <= not A1 and not B1 and  C1;
b <= not A1 and C1 and  D1;
b <= A1 and not B1 and  not C1;
c <= not A1 and not C1;
c <= not A1 and C1 and  D1;
c <= not A1 and B1 and  C1;
c <= A1 and not B1 and  not C1;
d <= not A1 and not B1 and C1;
d <= not A1 and C1 and not D1;
d <= not A1 and not B1 and not D1;
d <= not A1 and B1 and not C1 and D1;
d <= A1 and not B1 and not C1;
e <= not A1 and not B1 and not D1;
e <= not A1 and C1 and not D1;
e <= A1 and not B1 and not C1 and not D1;
f <= not A1 and not C1 and not D1;
f <= not A1 and B1 and not D1;
f <= not A1 and B1 and not C1;
f <= A1 and not B1 and not C1;
g <= not A1 and B1 and not C1;
g <= not A1 and not B1 and D1;
g <= not A1 and C1 and not D1;
g <= A1 and not B1 and not C1;
g <= not LT and not RBO2; 



END TypeArchitecture;
