// Logisim project AP3DeslocadorPronto.circ as structural Verilog
module main (
  input  Deslocador1bit,
  input  Deslocador2bit,
  input  in_3,
  input  in_4,
  input  in_5,
  input  in_6,
  output out_7,
  output out_8,
  output out_9,
  output out_10
);

  wire and_1_out, and_2_out, and_3_out, and_4_out, and_5_out, and_6_out, and_7_out, and_8_out, and_9_out,
       and_10_out, and_11_out, and_12_out, and_13_out, not_1_out, not_2_out, not_3_out, not_4_out, or_1_out,
       or_2_out, or_3_out, or_5_out, or_6_out;

  not not_1 (not_1_out, Deslocador1bit);
  not not_2 (not_2_out, Deslocador1bit);
  not not_3 (not_3_out, Deslocador1bit);
  not not_4 (not_4_out, Deslocador1bit);
  and and_1 (and_1_out, not_1_out, in_3);
  and and_2 (and_2_out, Deslocador1bit, in_4);
  and and_3 (and_3_out, not_2_out, in_4);
  and and_4 (and_4_out, Deslocador1bit, in_5);
  and and_5 (and_5_out, not_3_out, in_5);
  and and_6 (and_6_out, Deslocador1bit, in_6);
  and and_7 (and_7_out, not_4_out, in_6);
  and and_8 (and_8_out, Deslocador1bit, ~Deslocador1bit);  // AND_Gate
  and and_9 (and_9_out, in_5, ~in_3, ~in_4, ~in_6);  // AND_Gate
  and and_10 (and_10_out, ~in_3, in_6, ~in_4, ~in_5);  // AND_Gate
  and and_11 (and_11_out, in_5, in_6);
  and and_12 (and_12_out, in_5, in_6);
  or or_1 (or_1_out, and_1_out, and_2_out);
  or or_2 (or_2_out, and_3_out, and_4_out);
  or or_3 (or_3_out, and_5_out, and_6_out);
  or or_4 (out_10, and_7_out, and_8_out);
  or or_5 (or_5_out, and_9_out, and_11_out);
  or or_6 (or_6_out, and_10_out, and_12_out);
  and and_13 (and_13_out, Deslocador2bit, Deslocador1bit);
  Multiplexer multiplexer_1 (.in0(or_1_out), .in1(or_5_out), .out(out_7), .sel(and_13_out));
  Multiplexer multiplexer_2 (.in0(or_2_out), .in1(or_6_out), .out(out_8), .sel(and_13_out));
  Multiplexer multiplexer_3 (.in0(or_3_out), .in1(and_8_out), .out(out_9), .sel(and_13_out));
endmodule

// VHDL entity deslocador, as the project stores it:
--------------------------------------------------------------------------------
-- Project :
-- File    :
-- Autor   :
-- Date    :
--
--------------------------------------------------------------------------------
-- Description :
--
--------------------------------------------------------------------------------

LIBRARY ieee;
USE ieee.std_logic_1164.all;

ENTITY deslocador IS
  PORT (
  ------------------------------------------------------------------------------
  --Insert input ports below
    A          : IN  std_logic;
    B          : IN  std_logic;
    C          : IN  std_logic;
    D          : IN  std_logic;
    DL1        : IN  std_logic;
    DL2        : IN  std_logic;
  ------------------------------------------------------------------------------
  --Insert output ports below
    A1         : OUT std_logic;
    B1         : OUT std_logic;
    C1         : OUT std_logic;
    D1         : OUT std_logic;
    Seletor    : OUT std_logic
    );
END deslocador;

--------------------------------------------------------------------------------
--Complete your VHDL description below
--------------------------------------------------------------------------------

ARCHITECTURE TypeArchitecture OF deslocador IS

BEGIN

Seletor <= D2;
  case Seletor is
    when "0" => A1 <= ((not DL1 and A) or (DL1 and B));
    when "1" => A1 <= ((C and not A and not B and not D1) or (C and D1));
  end case;
  case Seletor is
    when "0" => B1 <= ( ( not DL1 and B) or (DL1 and C));
    when "1" => B1 <= ( ( not A and D1 and not B and not C) or (C and D1));
  end case;
   case Seletor is
    when "0" => C1 <= ( ( not DL1 and C) or (DL1 and D1));
    when "1" => C1 <= (DL1 and not DL1);
  end case;

D1 <= ( (not DL1 and D1) or (DL1 and not DL1);




END TypeArchitecture;
