// Logisim project AP3Normalizador.circ as structural Verilog
module main (
  input  in_1,
  input  in_2,
  input  in_3,
  input  in_4,
  output out_5,
  output out_6,
  output out_7,
  output out_8,
  output out_9
);

  wire and_1_out, and_2_out, and_3_out, and_4_out, and_5_out, and_6_out, and_7_out, and_8_out, and_9_out,
       and_10_out, and_11_out, and_12_out, and_13_out, and_14_out, and_15_out, and_16_out, and_17_out,
       and_18_out, and_19_out, DE2_out, DE_out, not_1_out, not_2_out, not_3_out, not_4_out, or_2_out,
       or_3_out, or_4_out, or_5_out, or_6_out, or_7_out, or_8_out, or_9_out, xor_1_out;

  and DE2 (DE2_out, ~in_1, ~in_2, in_3);  // AND_Gate
  and DE (DE_out, ~in_1, in_2);  // AND_Gate
  not not_1 (not_1_out, DE_out);
  not not_2 (not_2_out, DE_out);
  not not_3 (not_3_out, DE_out);
  not not_4 (not_4_out, DE_out);
  and and_1 (and_1_out, not_1_out, in_1);
  and and_2 (and_2_out, DE_out, in_2);
  and and_3 (and_3_out, not_2_out, in_2);
  and and_4 (and_4_out, DE_out, in_3);
  and and_5 (and_5_out, not_3_out, in_3);
  and and_6 (and_6_out, DE_out, in_4);
  and and_7 (and_7_out, not_4_out, in_4);
  and and_8 (and_8_out, DE_out, ~DE_out);  // AND_Gate
  and and_9 (and_9_out, in_2, ~in_3, ~in_4);  // AND_Gate
  and and_10 (and_10_out, in_1, ~in_3, ~in_4);  // AND_Gate
  and and_11 (and_11_out, ~in_1, in_3, ~in_4);  // AND_Gate
  and and_12 (and_12_out, in_1, in_3, ~in_4);  // AND_Gate
  and and_13 (and_13_out, in_1, ~in_2, ~in_4);  // AND_Gate
  or or_1 (out_9, in_1, in_2, in_3, in_4);
  and and_14 (and_14_out, in_3, ~in_1, ~in_2, ~in_4);  // AND_Gate
  and and_15 (and_15_out, ~in_1, in_4, ~in_2, ~in_3);  // AND_Gate
  and and_16 (and_16_out, in_3, in_4);
  and and_17 (and_17_out, in_3, in_4);
  and and_18 (and_18_out, ~in_3, ~in_2, ~in_1, in_4);  // AND_Gate
  or or_2 (or_2_out, and_9_out, and_10_out);
  or or_3 (or_3_out, and_11_out, and_12_out, and_13_out);
  and and_19 (and_19_out, ~DE_out, DE2_out);  // AND_Gate
  or or_4 (or_4_out, and_1_out, xor_1_out, and_2_out);
  or or_5 (or_5_out, and_3_out, and_4_out);
  or or_6 (or_6_out, and_5_out, and_6_out);
  or or_7 (or_7_out, and_7_out, and_8_out);
  or or_8 (or_8_out, and_14_out, and_16_out);
  or or_9 (or_9_out, and_15_out, and_17_out);
  ExactlyOne xor_1 (.out(xor_1_out), .in0(or_2_out), .in1(and_18_out), .in2(or_3_out));
  Multiplexer multiplexer_1 (.in0(or_4_out), .in1(or_8_out), .out(out_5), .sel(and_19_out));
  Multiplexer multiplexer_2 (.in0(or_5_out), .in1(or_9_out), .out(out_6), .sel(and_19_out));
  and and_20 (out_8, or_7_out, ~xor_1_out);  // AND_Gate
  Multiplexer multiplexer_3 (.in0(or_6_out), .in1(and_8_out), .out(out_7), .sel(and_19_out));
endmodule

// VHDL entity deslocador, as the project stores it:
--------------------------------------------------------------------------------
-- Project :
-- File    :
-- Autor   :
-- Date    :
--
--------------------------------------------------------------------------------
-- Description :
--
--------------------------------------------------------------------------------

LIBRARY ieee;
USE ieee.std_logic_1164.all;

ENTITY deslocador IS
  PORT (
  ------------------------------------------------------------------------------
  --Insert input ports below
    A         : IN  std_logic;
    B         : IN  std_logic;
    C         : IN  std_logic;
    D         : IN  std_logic;
    
  ------------------------------------------------------------------------------
  --Insert output ports below
    A1        : OUT std_logic;
    B1        : OUT std_logic;
    C1        : OUT std_logic;
    D1        : OUT std_logic;     
    Selector  : OUT std_logic  
      
    );
END deslocador;

--------------------------------------------------------------------------------
--Complete your VHDL description below
--------------------------------------------------------------------------------

ARCHITECTURE TypeArchitecture OF deslocador IS

BEGIN

Selector <= (B and A) and (not A and not B and C);
  case Selector is
    when "0" => A1 <= (A and (B and A)) OR (B and (B and A)) OR ( (not A and not B and not C and D) xor ((B and not C and not D) or (A and not C and not D)) xor ((not A and C and not D) or (A and C and not D) or (A and not B and not D));
    when "1" => A1 <= ((C and not A and not B and not D) or (C and D);
  end case;
  case Selector is
    when "0" => B1 <= ((not (B and A) and B) or ((B and A) and C));
    when "1" => B1 <= ((not A and D and not B and not C) or (C and D));
  end case;
    case Selector is
    when "0" => C1 <= (((B and A) and B) or ((B and A) and D);
    when "1" => C1 <= ((B and A) and not (B and A);
  end case;

D1 <= ( ( not (B and A) and D) or ( ( B and A) and not ( B and A) )) and not ( ( not C and not B and not A and D) xor ( ( B and not C and not D) or (A and not C and not D)) xor ( ( not A and C and not D) or (A and C and not D) or (A and not B and not D));



END TypeArchitecture;
