// Logisim project AP4ALU.circ as structural Verilog
module main (
  input  A7,
  input  A6,
  input  A5,
  input  A4,
  input  A3,
  input  A2,
  input  A1,
  input  A0,
  input  B7,
  input  B6,
  input  B5,
  input  B4,
  input  B3,
  input  B2,
  input  B1,
  input  B0,
  input  Subtr,
  input  UnLog,
  input  zeroANDouNORum,
  output CarryOut,
  output Overflow,
  output Sinal,
  output out_23,
  output out_24,
  output out_25,
  output out_26,
  output out_27,
  output out_28,
  output out_29,
  output out_30,
  output Zeros
);

  wire and_1_out, and_2_out, and_3_out, and_4_out, and_5_out, and_6_out, and_7_out, and_8_out,
       carrylockahead_1_s0, carrylockahead_1_s1, carrylockahead_1_s2, carrylockahead_1_s3,
       carrylockahead_1_s4, carrylockahead_1_s5, carrylockahead_1_s6, carrylockahead_1_s7, d2_1_a, d2_1_b,
       d2_1_c, d2_1_d, d2_1_e, d2_1_f, d2_1_g, d2_2_a, d2_2_b, d2_2_c, d2_2_d, d2_2_e, d2_2_f, d2_2_g,
       multiplexer_1_out, multiplexer_2_out, multiplexer_3_out, multiplexer_4_out, multiplexer_5_out,
       multiplexer_6_out, multiplexer_7_out, multiplexer_8_out, multiplexer_17_out, multiplexer_18_out,
       multiplexer_19_out, multiplexer_20_out, multiplexer_21_out, multiplexer_22_out, multiplexer_23_out,
       multiplexer_24_out, nor_1_out, nor_2_out, nor_3_out, nor_4_out, nor_5_out, nor_6_out, nor_7_out,
       nor_8_out, not_1_out, not_2_out, not_3_out, not_4_out, not_5_out, not_6_out, not_7_out, not_8_out,
       or_1_out, or_2_out;

  not not_1 (not_1_out, B0);
  not not_2 (not_2_out, B1);
  not not_3 (not_3_out, B2);
  not not_4 (not_4_out, B3);
  not not_5 (not_5_out, B4);
  not not_6 (not_6_out, B5);
  not not_7 (not_7_out, B6);
  not not_8 (not_8_out, B7);
  Multiplexer multiplexer_1 (.in0(B0), .in1(not_1_out), .out(multiplexer_1_out), .sel(Subtr));
  Multiplexer multiplexer_2 (.in0(B1), .in1(not_2_out), .out(multiplexer_2_out), .sel(Subtr));
  Multiplexer multiplexer_3 (.in0(B2), .in1(not_3_out), .out(multiplexer_3_out), .sel(Subtr));
  Multiplexer multiplexer_4 (.in0(B3), .in1(not_4_out), .out(multiplexer_4_out), .sel(Subtr));
  Multiplexer multiplexer_5 (.in0(B4), .in1(not_5_out), .out(multiplexer_5_out), .sel(Subtr));
  Multiplexer multiplexer_6 (.in0(B5), .in1(not_6_out), .out(multiplexer_6_out), .sel(Subtr));
  Multiplexer multiplexer_7 (.in0(B6), .in1(not_7_out), .out(multiplexer_7_out), .sel(Subtr));
  Multiplexer multiplexer_8 (.in0(B7), .in1(not_8_out), .out(multiplexer_8_out), .sel(Subtr));
  and and_1 (and_1_out, multiplexer_1_out, A0);
  and and_2 (and_2_out, multiplexer_2_out, A1);
  and and_3 (and_3_out, A2, multiplexer_3_out);
  and and_4 (and_4_out, multiplexer_4_out, A3);
  and and_5 (and_5_out, multiplexer_5_out, A4);
  and and_6 (and_6_out, multiplexer_6_out, A5);
  and and_7 (and_7_out, multiplexer_7_out, A6);
  and and_8 (and_8_out, multiplexer_8_out, A7);
  nor nor_1 (nor_1_out, multiplexer_1_out, A0);
  nor nor_2 (nor_2_out, multiplexer_2_out, A1);
  nor nor_3 (nor_3_out, A2, multiplexer_3_out);
  nor nor_4 (nor_4_out, A3, multiplexer_4_out);
  nor nor_5 (nor_5_out, multiplexer_5_out, A4);
  nor nor_6 (nor_6_out, multiplexer_6_out, A5);
  nor nor_7 (nor_7_out, multiplexer_7_out, A6);
  nor nor_8 (nor_8_out, multiplexer_8_out, A7);
  carrylockahead carrylockahead_1 (
    .A0(A0), .B0(multiplexer_1_out), .A1(A1), .B1(multiplexer_2_out), .A2(A2), .B2(multiplexer_3_out),
    .A3(A3), .B3(multiplexer_4_out), .A4(A4), .B4(multiplexer_5_out), .A5(A5), .B5(multiplexer_6_out),
    .A6(A6), .B6(multiplexer_7_out), .A7(A7), .B7(multiplexer_8_out), .Cin(Subtr), .C7(CarryOut),
    .S0(carrylockahead_1_s0), .S1(carrylockahead_1_s1), .S2(carrylockahead_1_s2), .S3(carrylockahead_1_s3),
    .S4(carrylockahead_1_s4), .S5(carrylockahead_1_s5), .S6(carrylockahead_1_s6), .S7(carrylockahead_1_s7));
  Multiplexer multiplexer_9 (.in0(carrylockahead_1_s0), .in1(multiplexer_17_out), .out(out_30), .sel(UnLog));
  Multiplexer multiplexer_10 (.in0(carrylockahead_1_s1), .in1(multiplexer_18_out), .out(out_29), .sel(UnLog));
  Multiplexer multiplexer_11 (.in0(carrylockahead_1_s2), .in1(multiplexer_19_out), .out(out_28), .sel(UnLog));
  Multiplexer multiplexer_12 (.in0(carrylockahead_1_s3), .in1(multiplexer_20_out), .out(out_27), .sel(UnLog));
  Multiplexer multiplexer_13 (.in0(carrylockahead_1_s4), .in1(multiplexer_21_out), .out(out_26), .sel(UnLog));
  Multiplexer multiplexer_14 (.in0(carrylockahead_1_s5), .in1(multiplexer_22_out), .out(out_25), .sel(UnLog));
  Multiplexer multiplexer_15 (.in0(carrylockahead_1_s6), .in1(multiplexer_23_out), .out(out_24), .sel(UnLog));
  Multiplexer multiplexer_16 (.in0(carrylockahead_1_s7), .in1(multiplexer_24_out), .out(out_23), .sel(UnLog));
  and and_9 (Overflow, CarryOut, out_23);
  or or_1 (or_1_out, out_30, out_29, out_28, out_27);
  or or_2 (or_2_out, out_26, out_25, out_24, out_23);
  d2 d2_1 (
    .D1(out_30), .C1(out_29), .B1(out_28), .A1(out_27), .a(d2_1_a), .b(d2_1_b), .c(d2_1_c), .d(d2_1_d),
    .e(d2_1_e), .f(d2_1_f), .g(d2_1_g));
  d2 d2_2 (
    .D1(out_26), .C1(out_25), .B1(out_24), .A1(out_23), .a(d2_2_a), .b(d2_2_b), .c(d2_2_c), .d(d2_2_d),
    .e(d2_2_e), .f(d2_2_f), .g(d2_2_g));
  or or_3 (Zeros, or_1_out, or_2_out);
  _7_Segment_Display u_7_segment_display_1 (
    .g(d2_2_g), .f(d2_2_f), .a(d2_2_a), .b(d2_2_b), .e(d2_2_e), .d(d2_2_d), .c(d2_2_c));  // open: dp
  _7_Segment_Display u_7_segment_display_2 (
    .g(d2_1_g), .f(d2_1_f), .a(d2_1_a), .b(d2_1_b), .e(d2_1_e), .d(d2_1_d), .c(d2_1_c));  // open: dp
  Multiplexer multiplexer_17 (.in0(and_1_out), .in1(nor_1_out), .out(multiplexer_17_out), .sel(zeroANDouNORum));
  Multiplexer multiplexer_18 (.in0(and_2_out), .in1(nor_2_out), .out(multiplexer_18_out), .sel(zeroANDouNORum));
  Multiplexer multiplexer_19 (.in0(and_3_out), .in1(nor_3_out), .out(multiplexer_19_out), .sel(zeroANDouNORum));
  Multiplexer multiplexer_20 (.in0(and_4_out), .in1(nor_4_out), .out(multiplexer_20_out), .sel(zeroANDouNORum));
  Multiplexer multiplexer_21 (.in0(and_5_out), .in1(nor_5_out), .out(multiplexer_21_out), .sel(zeroANDouNORum));
  Multiplexer multiplexer_22 (.in0(and_6_out), .in1(nor_6_out), .out(multiplexer_22_out), .sel(zeroANDouNORum));
  Multiplexer multiplexer_23 (.in0(and_7_out), .in1(nor_7_out), .out(multiplexer_23_out), .sel(zeroANDouNORum));
  Multiplexer multiplexer_24 (.in0(and_8_out), .in1(nor_8_out), .out(multiplexer_24_out), .sel(zeroANDouNORum));

  assign Sinal = out_23;
endmodule

// VHDL entity carrylockahead, as the project stores it:
--------------------------------------------------------------------------------
-- Project :
-- File    :
-- Autor   :
-- Date    :
--
--------------------------------------------------------------------------------
-- Description :
--
--------------------------------------------------------------------------------

LIBRARY ieee;
USE ieee.std_logic_1164.all;

ENTITY carrylockahead IS
  PORT (
  ------------------------------------------------------------------------------
  --Insert input ports below
    A0      : IN  std_logic;                    -- input bit example
    B0      : IN  std_logic; 
    A1      : IN  std_logic;                    -- input bit example
    B1      : IN  std_logic;  
    A2      : IN  std_logic;                    -- input bit example
    B2      : IN  std_logic;  
    A3      : IN  std_logic;                    -- input bit example
    B3      : IN  std_logic; 
    A4      : IN  std_logic;                    -- input bit example
    B4      : IN  std_logic; 
    A5      : IN  std_logic;                    -- input bit example
    B5      : IN  std_logic;  
    A6      : IN  std_logic;                    -- input bit example
    B6      : IN  std_logic;  
    A7      : IN  std_logic;                    -- input bit example
    B7      : IN  std_logic;
    Cin      : IN  std_logic; 
       
    
  ------------------------------------------------------------------------------
  --Insert output ports below 
    C7        : OUT std_logic;
    S0        : OUT std_logic; 
    S1        : OUT std_logic; 
    S2        : OUT std_logic; 
    S3        : OUT std_logic;
    S4        : OUT std_logic;
    S5        : OUT std_logic;   
    S6        : OUT std_logic; 
    S7	    : OUT std_logic
    
    );
END carrylockahead;

--------------------------------------------------------------------------------
--Complete your VHDL description below
--------------------------------------------------------------------------------

ARCHITECTURE TypeArchitecture OF carrylockahead IS

signal a : std_logic;
signal p0 : std_logic;
signal g0 : std_logic;
signal p1 : std_logic;
signal g1 : std_logic;
signal p2 : std_logic;
signal g2 : std_logic;
signal p3 : std_logic;
signal g3 : std_logic;
signal p4 : std_logic;
signal g4 : std_logic;
signal p5 : std_logic;
signal g5 : std_logic;
signal p6 : std_logic;
signal g6 : std_logic;
signal p7 : std_logic;
signal g7 : std_logic;


BEGIN

g0 <= A0 and B0;
p0 <= A0 xor B0;
g1 <= A1 and B1;
p1 <= A1 xor B1;
g2 <= A2 and B2;
p2 <= A2 xor B2;
g3 <= A3 and B3;
p3 <= A3 xor B3;
g4 <= A4 and B4;
p4 <= A4 xor B4;
g5 <= A5 and B5;
p5 <= A5 xor B5;
g6 <= A5 and B5;
p6 <= A6 xor B6;
g7 <= A7 and B7;
p7 <= A7 xor B7;

S0 <= p0 xor Cin;

S1 <= p1 xor (g0 or (p0 and Cin));

S2 <= p2 xor (g1 or (p1 and g0) or (p1 and p0 and Cin));

S3 <= p3 xor (g2 or (p2 and g1) or (p2 and p1 and g0) or (p2 and p1 and p0 and Cin));

S4 <= p4 xor (g3 or (p3 and g2) or (p3 and p2 and g1) or (p3 and p2 and p1 and g0) or (p3 and p2 and p1 and p0 and Cin));

S5 <= p5 xor (g4 or (p4 and g3) or (p4 and p3 and g2) or (p4 and p3 and p2 and g1) or (p4 and p3 and p2 and p1 and g0) or (p3 and p3 and p2 and p1 and p0 and Cin));
 
S6 <= p6 xor (g5 or (p5 and g4) or (p5 and p4 and g3) or (p5 and p4 and p3 and g2) or (p5 and p4 and p3 and p2 and g1) or (p5 and p4 and p3 and p2 and p1 and g0) or (p5 and p3 and p3 and p2 and p1 and p0 and Cin));

S7 <= p7 xor (g6 or (p6 and g5) or (p6 and p5 and g4) or (p6 and p5 and p4 and g3) or (p6 and p5 and p4 and p3 and g2) or (p6 and p5 and p4 and p3 and p2 and g1) or (p6 and p5 and p4 and p3 and p2 and p1 and g0) or (p6 and p5 and p3 and p3 and p2 and p1 and p0 and Cin));

C7 <= g7 or (p7 and g6) or (p7 and p6 and g5) or (p7 and p6 and p5 and g4) or (p7 and p6 and p5 and p4 and g3) or (p7 and p6 and p5 and p4 and p3 and g2) or (p7 and p6 and p5 and p4 and p3 and p2 and g1) or (p7 and p6 and p5 and p4 and p3 and p2 and p1 and g0) or (p7 and p6 and p5 and p3 and p3 and p2 and p1 and p0 and Cin);

END TypeArchitecture;

// VHDL entity d2, as the project stores it:
--------------------------------------------------------------------------------
-- Project :
-- File    :
-- Autor   :
-- Date    :
--
--------------------------------------------------------------------------------
-- Description :
--
--------------------------------------------------------------------------------

LIBRARY ieee;
USE ieee.std_logic_1164.all;

ENTITY d2 IS
  PORT (
  ------------------------------------------------------------------------------
  --Insert input ports below
    D1         : IN  std_logic;
    C1         : IN  std_logic;
    B1         : IN  std_logic;
    A1         : IN  std_logic;
  ------------------------------------------------------------------------------
  --Insert output ports below
    a          : OUT std_logic;
    b          : OUT std_logic;
    c          : OUT std_logic;
    d          : OUT std_logic;
    e          : OUT std_logic;
    f          : OUT std_logic;
    g          : OUT std_logic
    );
END d2;

--------------------------------------------------------------------------------
--Complete your VHDL description below
--------------------------------------------------------------------------------

ARCHITECTURE TypeArchitecture OF d2 IS

BEGIN
a <= (not A1 and not B1 and not C1 and not D1) or (not A1 and C1) or (not A1 and B1 and not C1 and D1) or (A1 and not C1 and not D1) or (A1 and not B1 and not C1) or (A1 and B1 and C1) or (A1 and C1 and not D1);
b <= (not A1 and not B1 and not C1) or (not A1 and not C1 and not D1) or (not A1 and not B1 and C1) or (not A1 and C1 and D1) or (A1 and not C1 and D1) or (A1 and not B1 and not C1) or (A1 and not B1 and C1 and not D1);
c <= (not A1 and not C1) or (not A1 and C1 and D1) or (not A1 and B1 and C1) or (A1 and not C1 and D1) or (A1 and not B1 and not C1) or (A1 and not B1 and C1);
d <= (not A1 and not B1 and not D1) or ( not A1 and not B1 and C1) or (B1 and C1 and not D1) or (B1 and not C1 and D1) or (A1 and not C1 and not D1) or (A1 and not B1 and C1 and D1);
e <= (not A1 and not B1 and not D1) or ( not A1 and C1 and not D1) or (A1 and C1) or (A1 and B1 and not C1) or (A1 and not B1 and not C1 and not D1);
f <= (A1 and C1) or (A1 and not B1 and not C1) or (A1 and not C1 and not D1) or (not A1 and B1 and not C1) or (not A1 and B1 and not D1) or (not A1 and not C1 and not D1);
g <= (A1 and C1) or (A1 and not B1 and not C1) or (A1 and not C1 and D1) or (not A1 and B1 and not C1) or (not A1 and not B1 and C1) or (not A1 and C1 and not D1);
END TypeArchitecture;
