// Logisim project AP5.circ as structural Verilog
module main (
  input  in_1,
  input  in_2,
  input  in_3,
  input  in_4,
  input  in_5,
  input  in_6,
  input  in_7,
  input  in_8,
  input  in_9,
  input  in_10,
  input  in_11,
  input  in_12,
  input  in_13,
  input  in_14,
  input  in_15,
  input  in_16,
  input  in_17,
  input  in_18,
  input  in_19,
  input  in_20,
  input  in_21,
  input  in_22,
  input  in_23,
  input  in_24,
  input  in_25,
  input  in_26,
  input  in_27,
  input  in_28,
  input  in_29,
  input  in_30,
  input  in_31,
  input  in_32,
  input  [1:0] _01___8x8,
  input  Subtrator,
  output out_35,
  output out_36,
  output out_37,
  output out_38,
  output out_39,
  output out_40,
  output out_41,
  output out_42,
  output out_43,
  output out_44,
  output out_45,
  output out_46,
  output out_47,
  output out_48,
  output out_49,
  output out_50
);

  wire sxtcarrylockahead_1_s0, sxtcarrylockahead_1_s1, sxtcarrylockahead_1_s2, sxtcarrylockahead_1_s3,
       sxtcarrylockahead_1_s4, sxtcarrylockahead_1_s5, sxtcarrylockahead_1_s6, sxtcarrylockahead_1_s7,
       sxtcarrylockahead_1_s8, sxtcarrylockahead_1_s9, sxtcarrylockahead_1_s10, sxtcarrylockahead_1_s11,
       sxtcarrylockahead_1_s12, sxtcarrylockahead_1_s13, sxtcarrylockahead_1_s14, sxtcarrylockahead_1_s15,
       sxtcarrylockahead_1_s17, sxtcarrylockahead_1_s18, sxtcarrylockahead_1_s19, sxtcarrylockahead_1_s20,
       sxtcarrylockahead_1_s21, sxtcarrylockahead_1_s22, sxtcarrylockahead_1_s23, sxtcarrylockahead_1_s24,
       sxtcarrylockahead_1_s25, sxtcarrylockahead_1_s26, sxtcarrylockahead_1_s27, sxtcarrylockahead_1_s28,
       sxtcarrylockahead_1_s29, sxtcarrylockahead_1_s30, sxtcarrylockahead_1_s31, sxtcarrylockahead_1_s32,
       sxtcarrylockahead_1_s34, sxtcarrylockahead_1_s35, sxtcarrylockahead_1_s36, sxtcarrylockahead_1_s37,
       sxtcarrylockahead_1_s38, sxtcarrylockahead_1_s39, sxtcarrylockahead_1_s40, sxtcarrylockahead_1_s41,
       sxtcarrylockahead_1_s42, sxtcarrylockahead_1_s43, sxtcarrylockahead_1_s44, sxtcarrylockahead_1_s45,
       sxtcarrylockahead_1_s46, sxtcarrylockahead_1_s47, sxtcarrylockahead_1_s48, sxtcarrylockahead_1_s49,
       sxtcarrylockahead_1_s51, sxtcarrylockahead_1_s52, sxtcarrylockahead_1_s53, sxtcarrylockahead_1_s54,
       sxtcarrylockahead_1_s55, sxtcarrylockahead_1_s56, sxtcarrylockahead_1_s57, sxtcarrylockahead_1_s58,
       sxtcarrylockahead_1_s59, sxtcarrylockahead_1_s60, sxtcarrylockahead_1_s61, sxtcarrylockahead_1_s62,
       sxtcarrylockahead_1_s63, sxtcarrylockahead_1_s64, sxtcarrylockahead_1_s65, sxtcarrylockahead_1_s66;

  SXTcarrylockahead sxtcarrylockahead_1 (
    .A0(in_16), .B0(in_24), .A1(in_15), .B1(in_23), .A2(in_14), .B2(in_22), .A3(in_13), .B3(in_21),
    .A4(in_12), .B4(in_20), .A5(in_11), .B5(in_19), .A6(in_10), .B6(in_18), .A7(in_9), .B7(in_17), .A8(in_8),
    .B8(in_32), .A9(in_7), .B9(in_31), .A10(in_6), .B10(in_30), .A11(in_5), .B11(in_29), .A12(in_4),
    .B12(in_28), .A13(in_3), .B13(in_27), .A14(in_2), .B14(in_26), .A15(in_1), .B15(in_25), .M(Subtrator),
    .Cin(Subtrator), .S0(sxtcarrylockahead_1_s0), .S1(sxtcarrylockahead_1_s1), .S2(sxtcarrylockahead_1_s2),
    .S3(sxtcarrylockahead_1_s3), .S4(sxtcarrylockahead_1_s4), .S5(sxtcarrylockahead_1_s5),
    .S6(sxtcarrylockahead_1_s6), .S7(sxtcarrylockahead_1_s7), .S8(sxtcarrylockahead_1_s8),
    .S9(sxtcarrylockahead_1_s9), .S10(sxtcarrylockahead_1_s10), .S11(sxtcarrylockahead_1_s11),
    .S12(sxtcarrylockahead_1_s12), .S13(sxtcarrylockahead_1_s13), .S14(sxtcarrylockahead_1_s14),
    .S15(sxtcarrylockahead_1_s15), .S34(sxtcarrylockahead_1_s34), .S35(sxtcarrylockahead_1_s35),
    .S36(sxtcarrylockahead_1_s36), .S37(sxtcarrylockahead_1_s37), .S38(sxtcarrylockahead_1_s38),
    .S39(sxtcarrylockahead_1_s39), .S40(sxtcarrylockahead_1_s40), .S41(sxtcarrylockahead_1_s41),
    .S42(sxtcarrylockahead_1_s42), .S43(sxtcarrylockahead_1_s43), .S44(sxtcarrylockahead_1_s44),
    .S45(sxtcarrylockahead_1_s45), .S46(sxtcarrylockahead_1_s46), .S47(sxtcarrylockahead_1_s47),
    .S48(sxtcarrylockahead_1_s48), .S49(sxtcarrylockahead_1_s49), .S51(sxtcarrylockahead_1_s51),
    .S52(sxtcarrylockahead_1_s52), .S53(sxtcarrylockahead_1_s53), .S54(sxtcarrylockahead_1_s54),
    .S55(sxtcarrylockahead_1_s55), .S56(sxtcarrylockahead_1_s56), .S57(sxtcarrylockahead_1_s57),
    .S58(sxtcarrylockahead_1_s58), .S59(sxtcarrylockahead_1_s59), .S60(sxtcarrylockahead_1_s60),
    .S61(sxtcarrylockahead_1_s61), .S62(sxtcarrylockahead_1_s62), .S63(sxtcarrylockahead_1_s63),
    .S64(sxtcarrylockahead_1_s64), .S65(sxtcarrylockahead_1_s65), .S66(sxtcarrylockahead_1_s66),
    .S17(sxtcarrylockahead_1_s17), .S18(sxtcarrylockahead_1_s18), .S19(sxtcarrylockahead_1_s19),
    .S20(sxtcarrylockahead_1_s20), .S21(sxtcarrylockahead_1_s21), .S22(sxtcarrylockahead_1_s22),
    .S23(sxtcarrylockahead_1_s23), .S24(sxtcarrylockahead_1_s24), .S25(sxtcarrylockahead_1_s25),
    .S26(sxtcarrylockahead_1_s26), .S27(sxtcarrylockahead_1_s27), .S28(sxtcarrylockahead_1_s28),
    .S29(sxtcarrylockahead_1_s29), .S30(sxtcarrylockahead_1_s30), .S31(sxtcarrylockahead_1_s31),
    .S32(sxtcarrylockahead_1_s32));
  Multiplexer #(.select(2)) multiplexer_1 (
    .in0(sxtcarrylockahead_1_s15), .in1(sxtcarrylockahead_1_s49), .in2(sxtcarrylockahead_1_s66),
    .in3(sxtcarrylockahead_1_s32), .out(out_35), .sel(_01___8x8));
  Multiplexer #(.select(2)) multiplexer_2 (
    .in0(sxtcarrylockahead_1_s14), .in1(sxtcarrylockahead_1_s48), .in2(sxtcarrylockahead_1_s65),
    .in3(sxtcarrylockahead_1_s31), .out(out_36), .sel(_01___8x8));
  Multiplexer #(.select(2)) multiplexer_3 (
    .in0(sxtcarrylockahead_1_s13), .in1(sxtcarrylockahead_1_s47), .in2(sxtcarrylockahead_1_s64),
    .in3(sxtcarrylockahead_1_s30), .out(out_37), .sel(_01___8x8));
  Multiplexer #(.select(2)) multiplexer_4 (
    .in0(sxtcarrylockahead_1_s12), .in1(sxtcarrylockahead_1_s46), .in2(sxtcarrylockahead_1_s63),
    .in3(sxtcarrylockahead_1_s29), .out(out_38), .sel(_01___8x8));
  Multiplexer #(.select(2)) multiplexer_5 (
    .in0(sxtcarrylockahead_1_s11), .in1(sxtcarrylockahead_1_s45), .in2(sxtcarrylockahead_1_s62),
    .in3(sxtcarrylockahead_1_s28), .out(out_39), .sel(_01___8x8));
  Multiplexer #(.select(2)) multiplexer_6 (
    .in0(sxtcarrylockahead_1_s10), .in1(sxtcarrylockahead_1_s44), .in2(sxtcarrylockahead_1_s61),
    .in3(sxtcarrylockahead_1_s27), .out(out_40), .sel(_01___8x8));
  Multiplexer #(.select(2)) multiplexer_7 (
    .in0(sxtcarrylockahead_1_s9), .in1(sxtcarrylockahead_1_s43), .in2(sxtcarrylockahead_1_s60),
    .in3(sxtcarrylockahead_1_s26), .out(out_41), .sel(_01___8x8));
  Multiplexer #(.select(2)) multiplexer_8 (
    .in0(sxtcarrylockahead_1_s8), .in1(sxtcarrylockahead_1_s42), .in2(sxtcarrylockahead_1_s59),
    .in3(sxtcarrylockahead_1_s25), .out(out_42), .sel(_01___8x8));
  Multiplexer #(.select(2)) multiplexer_9 (
    .in0(sxtcarrylockahead_1_s7), .in1(sxtcarrylockahead_1_s41), .in2(sxtcarrylockahead_1_s58),
    .in3(sxtcarrylockahead_1_s24), .out(out_43), .sel(_01___8x8));
  Multiplexer #(.select(2)) multiplexer_10 (
    .in0(sxtcarrylockahead_1_s6), .in1(sxtcarrylockahead_1_s40), .in2(sxtcarrylockahead_1_s57),
    .in3(sxtcarrylockahead_1_s23), .out(out_44), .sel(_01___8x8));
  Multiplexer #(.select(2)) multiplexer_11 (
    .in0(sxtcarrylockahead_1_s5), .in1(sxtcarrylockahead_1_s39), .in2(sxtcarrylockahead_1_s56),
    .in3(sxtcarrylockahead_1_s22), .out(out_45), .sel(_01___8x8));
  Multiplexer #(.select(2)) multiplexer_12 (
    .in0(sxtcarrylockahead_1_s4), .in1(sxtcarrylockahead_1_s38), .in2(sxtcarrylockahead_1_s55),
    .in3(sxtcarrylockahead_1_s21), .out(out_46), .sel(_01___8x8));
  Multiplexer #(.select(2)) multiplexer_13 (
    .in0(sxtcarrylockahead_1_s3), .in1(sxtcarrylockahead_1_s37), .in2(sxtcarrylockahead_1_s54),
    .in3(sxtcarrylockahead_1_s20), .out(out_47), .sel(_01___8x8));
  Multiplexer #(.select(2)) multiplexer_14 (
    .in0(sxtcarrylockahead_1_s2), .in1(sxtcarrylockahead_1_s36), .in2(sxtcarrylockahead_1_s53),
    .in3(sxtcarrylockahead_1_s19), .out(out_48), .sel(_01___8x8));
  Multiplexer #(.select(2)) multiplexer_15 (
    .in0(sxtcarrylockahead_1_s1), .in1(sxtcarrylockahead_1_s35), .in2(sxtcarrylockahead_1_s52),
    .in3(sxtcarrylockahead_1_s18), .out(out_49), .sel(_01___8x8));
  Multiplexer #(.select(2)) multiplexer_16 (
    .in0(sxtcarrylockahead_1_s0), .in1(sxtcarrylockahead_1_s34), .in2(sxtcarrylockahead_1_s51),
    .in3(sxtcarrylockahead_1_s17), .out(out_50), .sel(_01___8x8));

  // Notes on the sheet:
  //   A
  //   B
  //   00 : 16x16
  //   10 : 4x4
  //   11 : 2x2
endmodule

// VHDL entity SXTcarrylockahead, as the project stores it:
--------------------------------------------------------------------------------
-- Project :
-- File    :
-- Autor   :
-- Date    :
--
--------------------------------------------------------------------------------
-- Description :
--
--------------------------------------------------------------------------------

LIBRARY ieee;
USE ieee.std_logic_1164.all;

ENTITY SXTcarrylockahead IS
  PORT (
  ------------------------------------------------------------------------------
  --Insert input ports below
    A0      : IN  std_logic;                    -- input bit example
    B0      : IN  std_logic; 
    A1      : IN  std_logic;                    -- input bit example
    B1      : IN  std_logic;  
    A2      : IN  std_logic;                    -- input bit example
    B2      : IN  std_logic;  
    A3      : IN  std_logic;                    -- input bit example
    B3      : IN  std_logic; 
    A4      : IN  std_logic;                    -- input bit example
    B4      : IN  std_logic; 
    A5      : IN  std_logic;                    -- input bit example
    B5      : IN  std_logic;  
    A6      : IN  std_logic;                    -- input bit example
    B6      : IN  std_logic;  
    A7      : IN  std_logic;                    -- input bit example
    B7      : IN  std_logic;
    A8      : IN  std_logic;                    -- input bit example
    B8      : IN  std_logic;
    A9      : IN  std_logic;                    -- input bit example
    B9      : IN  std_logic;
    A10      : IN  std_logic;                    -- input bit example
    B10      : IN  std_logic;
    A11      : IN  std_logic;                    -- input bit example
    B11      : IN  std_logic;
    A12      : IN  std_logic;                    -- input bit example
    B12      : IN  std_logic;
    A13      : IN  std_logic;                    -- input bit example
    B13      : IN  std_logic;
    A14      : IN  std_logic;                    -- input bit example
    B14      : IN  std_logic;
    A15      : IN  std_logic;                    -- input bit example
    B15      : IN  std_logic;
    M        : IN  std_logic;
    Cin      : IN  std_logic; 
       
    
  ------------------------------------------------------------------------------
  --Insert output ports below
 
    
    S0        : OUT std_logic; 
    S1        : OUT std_logic; 
    S2        : OUT std_logic; 
    S3        : OUT std_logic;
    S4        : OUT std_logic;
    S5        : OUT std_logic;   
    S6        : OUT std_logic; 
    S7	    : OUT std_logic;
    S8	    : OUT std_logic;
    S9	    : OUT std_logic;
    S10	    : OUT std_logic;
    S11	    : OUT std_logic;
    S12	    : OUT std_logic;
    S13	    : OUT std_logic;
    S14	    : OUT std_logic;
    S15	    : OUT std_logic;
    S34	    : OUT std_logic;
    S35	    : OUT std_logic;
    S36	    : OUT std_logic;
    S37	    : OUT std_logic;
    S38	    : OUT std_logic;
    S39	    : OUT std_logic;
    S40	    : OUT std_logic;
    S41	    : OUT std_logic;
    S42	    : OUT std_logic;
    S43	    : OUT std_logic;
    S44	    : OUT std_logic;
    S45	    : OUT std_logic;
    S46	    : OUT std_logic;
    S47	    : OUT std_logic;
    S48	    : OUT std_logic;
    S49	    : OUT std_logic;
    S51	    : OUT std_logic;
    S52	    : OUT std_logic;
    S53	    : OUT std_logic;
    S54	    : OUT std_logic;
    S55	    : OUT std_logic;
    S56	    : OUT std_logic;
    S57	    : OUT std_logic;
    S58	    : OUT std_logic;
    S59	    : OUT std_logic;
    S60	    : OUT std_logic;
    S61	    : OUT std_logic;
    S62	    : OUT std_logic;
    S63	    : OUT std_logic;
    S64	    : OUT std_logic;
    S65	    : OUT std_logic;
    S66	    : OUT std_logic;
    S17	    : OUT std_logic;
    S18	    : OUT std_logic;
    S19	    : OUT std_logic;
    S20	    : OUT std_logic;
    S21	    : OUT std_logic;
    S22	    : OUT std_logic;
    S23	    : OUT std_logic;
    S24	    : OUT std_logic;
    S25	    : OUT std_logic;
    S26	    : OUT std_logic;
    S27	    : OUT std_logic;
    S28	    : OUT std_logic;
    S29	    : OUT std_logic;
    S30	    : OUT std_logic;
    S31	    : OUT std_logic;
    S32	    : OUT std_logic
    
    
 
    
    );
END SXTcarrylockahead;

--------------------------------------------------------------------------------
--Complete your VHDL description below
--------------------------------------------------------------------------------

ARCHITECTURE TypeArchitecture OF SXTcarrylockahead IS

signal a : std_logic;
signal p0 : std_logic;
signal g0 : std_logic;
signal p1 : std_logic;
signal g1 : std_logic;
signal p2 : std_logic;
signal g2 : std_logic;
signal p3 : std_logic;
signal g3 : std_logic;
signal p4 : std_logic;
signal g4 : std_logic;
signal p5 : std_logic;
signal g5 : std_logic;
signal p6 : std_logic;
signal g6 : std_logic;
signal p7 : std_logic;
signal g7 : std_logic;
signal p8 : std_logic;
signal g8 : std_logic;
signal p9 : std_logic;
signal g9 : std_logic;
signal p10 : std_logic;
signal g10 : std_logic;
signal p11 : std_logic;
signal g11 : std_logic;
signal p12 : std_logic;
signal g12 : std_logic;
signal p13 : std_logic;
signal g13 : std_logic;
signal p14 : std_logic;
signal g14 : std_logic;
signal p15 : std_logic;
signal g15 : std_logic;

signal q0 : std_logic;
signal h0 : std_logic;
signal q1 : std_logic;
signal h1 : std_logic;
signal q2 : std_logic;
signal h2 : std_logic;
signal q3 : std_logic;
signal h3 : std_logic;
signal q4 : std_logic;
signal h4 : std_logic;
signal q5 : std_logic;
signal h5 : std_logic;
signal q6 : std_logic;
signal h6 : std_logic;
signal q7 : std_logic;
signal h7 : std_logic;
signal q8 : std_logic;
signal h8 : std_logic;
signal q9 : std_logic;
signal h9 : std_logic;
signal q10 : std_logic;
signal h10 : std_logic;
signal q11 : std_logic;
signal h11 : std_logic;
signal q12 : std_logic;
signal h12 : std_logic;
signal q13 : std_logic;
signal h13 : std_logic;
signal q14 : std_logic;
signal h14 : std_logic;
signal q15 : std_logic;
signal h15 : std_logic;

signal r0 : std_logic;
signal i0 : std_logic;
signal r1 : std_logic;
signal i1 : std_logic;
signal r2 : std_logic;
signal i2 : std_logic;
signal r3 : std_logic;
signal i3 : std_logic;
signal r4 : std_logic;
signal i4 : std_logic;
signal r5 : std_logic;
signal i5 : std_logic;
signal r6 : std_logic;
signal i6 : std_logic;
signal r7 : std_logic;
signal i7 : std_logic;
signal r8 : std_logic;
signal i8 : std_logic;
signal r9 : std_logic;
signal i9 : std_logic;
signal r10 : std_logic;
signal i10 : std_logic;
signal r11 : std_logic;
signal i11 : std_logic;
signal r12 : std_logic;
signal i12 : std_logic;
signal r13 : std_logic;
signal i13 : std_logic;
signal r14 : std_logic;
signal i14 : std_logic;
signal r15 : std_logic;
signal i15 : std_logic;

BEGIN

g0 <= A0 and (B0 xor M);
p0 <= A0 xor (B0 xor M);

g1 <= A1 and (B1 xor M);
p1 <= A1 xor (B1 xor M);

g2 <= A2 and (B2 xor M);
p2 <= A2 xor (B2 xor M);

g3 <= A3 and (B3 xor M);
p3 <= A3 xor (B3 xor M);

g4 <= A4 and (B4 xor M);
p4 <= A4 xor (B4 xor M);

g5 <= A5 and (B5 xor M);
p5 <= A5 xor (B5 xor M);

g6 <= A6 and (B6 xor M);
p6 <= A6 xor (B6 xor M);

g7 <= A7 and (B7 xor M);
p7 <= A7 xor (B7 xor M);

g8 <= A8 and (B8 xor M);
p8 <= A8 xor (B8 xor M);

g9 <= A9 and (B9 xor M);
p9 <= A9 xor (B9 xor M);

g10 <= A10 and (B10 xor M);
p10 <= A10 xor (B10 xor M);

g11 <= A11 and (B11 xor M);
p11 <= A11 xor (B11 xor M);

g12 <= A12 and (B12 xor M);
p12 <= A12 xor (B12 xor M);

g13 <= A13 and (B13 xor M);
p13 <= A13 xor (B13 xor M);

g14 <= A14 and (B14 xor M);
p14 <= A14 xor (B14 xor M);

g15 <= A15 and (B15 xor M);
p15 <= A15 xor (B15 xor M);



h0 <= A0 and (B0 xor M);
q0 <= A0 xor (B0 xor M);

h1 <= A1 and (B1 xor M);
q1 <= A1 xor (B1 xor M);

h2 <= A2 and (B2 xor M);
q2 <= A2 xor (B2 xor M);

h3 <= A3 and (B3 xor M);
q3 <= A3 xor (B3 xor M);

h4 <= A4 and (B4 xor M);
q4 <= A4 xor (B4 xor M);

h5 <= A5 and (B5 xor M);
q5 <= A5 xor (B5 xor M);

h6 <= A6 and (B6 xor M);
q6 <= A6 xor (B6 xor M);

h7 <= A7 and (B7 xor M);
q7 <= A7 xor (B7 xor M);

h8 <= B8 and (A8 xor M);
q8 <= B8 xor (A8 xor M);

h9 <= B9 and (A9 xor M);
q9 <= B9 xor (A9 xor M);

h10 <= B10 and (A10 xor M);
q10 <= B10 xor (A10 xor M);

h11 <= B11 and (A11 xor M);
q11 <= B11 xor (A11 xor M);

h12 <= B12 and (A12 xor M);
q12 <= B12 xor (A12 xor M);

h13 <= B13 and (A13 xor M);
q13 <= B13 xor (A13 xor M);

h14 <= B14 and (A14 xor M);
q14 <= B14 xor (A14 xor M);

h15 <= B15 and (A15 xor M);
q15 <= B15 xor (A15 xor M);


i0 <= A0 and B0;
r0 <= A0 xor B0;

i1 <= A2 and B2;
r1 <= A2 xor B2;

i2 <= A4 and B4;
r2 <= A4 xor B4;

i3 <= A6 and B6;
r3 <= A6 xor B6;

i4 <= A8 and B8;
r4 <= A8 xor B8;

i5 <= A10 and B10;
r5 <= A10 xor B10;

i6 <= A12 and B12;
r6 <= A12 xor B12;

i7 <= A14 and B14;
r7 <= A14 xor B14;

i8 <= B1 and A1;
r8 <= B1 xor A1;

i9 <= B3 and A3;
r9 <= B3 xor A3;

i10 <= B5 and A5;
r10 <= B5 xor A5;

i11 <= B7 and A7; 
r11 <= B7 xor A7;

i12 <= B9 and A9;
r12 <= B9 xor A9;

i13 <= B11 and A11;
r13 <= B11 xor A11;

i14 <= B13 and A13;
r14 <= B13 xor A13;

i15 <= B15 and A15;
r15 <= B15 xor A15;


S0 <= p0 xor Cin;

S1 <= p1 xor (g0 or (p0 and Cin));

S2 <= p2 xor (g1 or (p1 and g0) or (p1 and p0 and Cin));

S3 <= p3 xor (g2 or (p2 and g1) or (p2 and p1 and g0) or (p2 and p1 and p0 and Cin));

S4 <= p4 xor (g3 or (p3 and g2) or (p3 and p2 and g1) or (p3 and p2 and p1 and g0) or (p3 and p2 and p1 and p0 and Cin));

S5 <= p5 xor (g4 or (p4 and g3) or (p4 and p3 and g2) or (p4 and p3 and p2 and g1) or (p4 and p3 and p2 and p1 and g0) or (p3 and p3 and p2 and p1 and p0 and Cin));
 
S6 <= p6 xor (g5 or (p5 and g4) or (p5 and p4 and g3) or (p5 and p4 and p3 and g2) or (p5 and p4 and p3 and p2 and g1) or (p5 and p4 and p3 and p2 and p1 and g0) or (p5 and p3 and p3 and p2 and p1 and p0 and Cin));

S7 <= p7 xor (g6 or (p6 and g5) or (p6 and p5 and g4) or (p6 and p5 and p4 and g3) or (p6 and p5 and p4 and p3 and g2) or (p6 and p5 and p4 and p3 and p2 and g1) or (p6 and p5 and p4 and p3 and p2 and p1 and g0) or (p6 and p5 and p3 and p3 and p2 and p1 and p0 and Cin));

S8 <=  p8 xor (g7 or (p7 and g6) or (p7 and p6 and g5) or (p7 and p6 and p5 and g4) or (p7 and p6 and p5 and p4 and g3) or (p7 and p6 and p5 and p4 and p3 and g2) or (p7 and p6 and p5 and p4 and p3 and p2 and g1) or (p7 and p6 and p5 and p4 and p3 and p2 and p1 and g0) or (p7 and p6 and p5 and p3 and p3 and p2 and p1 and p0 and Cin));

S9 <= p9 xor (g8 or (p8 and g7) or (p8 and p7 and g6) or (p8 and p7 and p6 and g5) or (p8 and p7 and p6 and p5 and g4) or (p8 and p7 and p6 and p5 and p4 and g3) or (p8 and p7 and p6 and p5 and p4 and p3 and g2) or (p8 and p7 and p6 and p5 and p4 and p3 and p2 and g1) or (p8 and p7 and p6 and p5 and p4 and p3 and p2 and p1 and g0) or (p8 and p7 and p6 and p5 and p3 and p3 and p2 and p1 and p0 and Cin));

S10 <= p10 xor (g9 or (p9 and g8) or (p9 and p8 and g7) or (p9 and p8 and p7 and g6) or (p9 and p8 and p7 and p6 and g5) or (p9 and p8 and p7 and p6 and p5 and g4) or (p9 and p8 and p7 and p6 and p5 and p4 and g3) or (p9 and p8 and p7 and p6 and p5 and p4 and p3 and g2) or (p9 and p8 and p7 and p6 and p5 and p4 and p3 and p2 and g1) or (p9 and p8 and p7 and p6 and p5 and p4 and p3 and p2 and p1 and g0) or (p9 and p8 and p7 and p6 and p5 and p3 and p3 and p2 and p1 and p0 and Cin));

S11 <= p11 xor (g10 or (p10 and g9) or (p10 and p9 and g8) or (p10 and p9 and p8 and g7) or (p10 and p9 and p8 and p7 and g6) or (p10 and p9 and p8 and p7 and p6 and g5) or (p10 and p9 and p8 and p7 and p6 and p5 and g4) or (p10 and p9 and p8 and p7 and p6 and p5 and p4 and g3) or (p10 and p9 and p8 and p7 and p6 and p5 and p4 and p3 and g2) or (p10 and p9 and p8 and p7 and p6 and p5 and p4 and p3 and p2 and g1) or (p10 and p9 and p8 and p7 and p6 and p5 and p4 and p3 and p2 and p1 and g0) or (p9 and p8 and p7 and p6 and p5 and p3 and p3 and p2 and p1 and p0 and Cin));

S12 <= p12 xor (g11 or (p11 and g10) or (p11 and p10 and g9) or (p11 and p10 and p9 and g8) or (p11 and p10 and p9 and p8 and g7) or (p11 and p10 and p9 and p8 and p7 and g6) or (p11 and p10 and p9 and p8 and p7 and p6 and g5) or (p11 and p10 and p9 and p8 and p7 and p6 and p5 and g4) or (p11 and p10 and p9 and p8 and p7 and p6 and p5 and p4 and g3) or (p11 and p10 and p9 and p8 and p7 and p6 and p5 and p4 and p3 and g2) or (p11 and p10 and p9 and p8 and p7 and p6 and p5 and p4 and p3 and p2 and g1) or (p11 and p10 and p9 and p8 and p7 and p6 and p5 and p4 and p3 and p2 and p1 and g0) or (p11 and p9 and p8 and p7 and p6 and p5 and p3 and p3 and p2 and p1 and p0 and Cin));

S13 <= p13 xor (g12 or (p12 and g11) or (p12 and p11 and g10) or (p12 and p11 and p10 and g9) or (p12 and p11 and p10 and p9 and g8) or (p12 and p11 and p10 and p9 and p8 and g7) or (p12 and p11 and p10 and p9 and p8 and p7 and g6) or (p12 and p11 and p10 and p9 and p8 and p7 and p6 and g5) or (p12 and p11 and p10 and p9 and p8 and p7 and p6 and p5 and g4) or (p12 and p11 and p10 and p9 and p8 and p7 and p6 and p5 and p4 and g3) or (p12 and p11 and p10 and p9 and p8 and p7 and p6 and p5 and p4 and p3 and g2) or (p12 and p11 and p10 and p9 and p8 and p7 and p6 and p5 and p4 and p3 and p2 and g1) or (p12 and p11 and p10 and p9 and p8 and p7 and p6 and p5 and p4 and p3 and p2 and p1 and g0) or (p12 and p11 and p9 and p8 and p7 and p6 and p5 and p3 and p3 and p2 and p1 and p0 and Cin));

S14 <= p14 xor (g13 or (p13 and g12) or (p13 and p12 and g11) or (p13 and p12 and p11 and g10) or (p13 and p12 and p11 and p10 and g9) or (p13 and p12 and p11 and p10 and p9 and g8) or (p13 and p12 and p11 and p10 and p9 and p8 and g7) or (p13 and p12 and p11 and p10 and p9 and p8 and p7 and g6) or (p13 and p12 and p11 and p10 and p9 and p8 and p7 and p6 and g5) or (p13 and p12 and p11 and p10 and p9 and p8 and p7 and p6 and p5 and g4) or (p13 and p12 and p11 and p10 and p9 and p8 and p7 and p6 and p5 and p4 and g3) or (p13 and p12 and p11 and p10 and p9 and p8 and p7 and p6 and p5 and p4 and p3 and g2) or (p13 and p12 and p11 and p10 and p9 and p8 and p7 and p6 and p5 and p4 and p3 and p2 and g1) or (p13 and p12 and p11 and p10 and p9 and p8 and p7 and p6 and p5 and p4 and p3 and p2 and p1 and g0) or (p13 and p12 and p11 and p9 and p8 and p7 and p6 and p5 and p3 and p3 and p2 and p1 and p0 and Cin));

S15 <= p8 xor (g14 or (p14 and g13) or (p14 and p13 and g12) or (p14 and p13 and p12 and g11) or (p14 and p13 and p12 and p11 and g10) or (p14 and p13 and p12 and p11 and p10 and g9) or (p14 and p13 and p12 and p11 and p10 and p9 and g8) or (p14 and p13 and p12 and p11 and p10 and p9 and p8 and g7) or (p14 and p13 and p12 and p11 and p10 and p9 and p8 and p7 and g6) or (p14 and p13 and p12 and p11 and p10 and p9 and p8 and p7 and p6 and g5) or (p14 and p13 and p12 and p11 and p10 and p9 and p8 and p7 and p6 and p5 and g4) or (p14 and p13 and p12 and p11 and p10 and p9 and p8 and p7 and p6 and p5 and p4 and g3) or (p14 and p13 and p12 and p11 and p10 and p9 and p8 and p7 and p6 and p5 and p4 and p3 and g2) or (p14 and p13 and p12 and p11 and p10 and p9 and p8 and p7 and p6 and p5 and p4 and p3 and p2 and g1) or (p14 and p13 and p12 and p11 and p10 and p9 and p8 and p7 and p6 and p5 and p4 and p3 and p2 and p1 and g0) or (p14 and p13 and p12 and p11 and p9 and p8 and p7 and p6 and p5 and p3 and p3 and p2 and p1 and p0 and Cin));

S34 <= q0 xor Cin;

S35 <= q1 xor (h0 or (q0 and Cin));

S36 <= q2 xor (h1 or (q1 and h0) or (q1 and h0 and Cin));

S37 <= q3 xor (h2 or (q2 and h1) or (q2 and q1 and h0) or (q2 and q1 and q0 and Cin));

S38 <= q4 xor (h3 or (q3 and h2) or (q3 and q2 and h1) or (q3 and q2 and q1 and h0) or (q3 and q2 and q1 and q0 and Cin));

S39 <= q5 xor (h4 or (q4 and h3) or (q4 and q3 and h2) or (q4 and q3 and q2 and h1) or (q4 and q3 and q2 and q1 and h0) or (q3 and q3 and q2 and q1 and q0 and Cin));
 
S40 <= q6 xor (h5 or (q5 and h4) or (q5 and q4 and h3) or (q5 and q4 and q3 and h2) or (q5 and q4 and q3 and q2 and h1) or (q5 and q4 and q3 and q2 and q1 and h0) or (q5 and q3 and q3 and q2 and q1 and q0 and Cin));

S41 <= q7 xor (h6 or (q6 and h5) or (q6 and q5 and h4) or (q6 and q5 and q4 and h3) or (q6 and q5 and q4 and q3 and h2) or (q6 and q5 and q4 and q3 and q2 and h1) or (q6 and q5 and q4 and q3 and q2 and q1 and h0) or (q6 and q5 and q3 and q3 and q2 and q1 and q0 and Cin));

S42 <=  q8 xor Cin;

S43 <= q9 xor (h8 or (q8 and Cin));

S44 <= q10 xor (h9 or (q9 and h8) or (q9 and q8 and Cin));

S45 <= q11 xor (h10 or (q10 and h9) or (q10 and q9 and h8) or (q10 and q9 and q8 and Cin));

S46 <= q12 xor (h11 or (q11 and h10) or (q11 and q10 and h9) or (q11 and q10 and q9 and h8) or (q11 and q10 and q9 and q8 and Cin));

S47 <= q13 xor (h12 or (q12 and h11) or (q12 and q11 and h10) or (q12 and q11 and q10 and h9) or (q12 and q11 and q10 and q9 and h8) or (q11 and q11 and q10 and q9 and q8 and Cin));

S48 <= q14 xor (h13 or (q13 and h12) or (q13 and q12 and h11) or (q13 and q12 and q11 and h10) or (q13 and q12 and q11 and q10 and h9) or (q13 and q12 and q11 and q10 and q9 and h8) or (q13 and q11 and q11 and q10 and q9 and q8 and Cin));

S49 <= q8 xor (h14 or (q14 and h13) or (q14 and q13 and h12) or (q14 and q13 and q12 and h11) or (q14 and q13 and q12 and q11 and h10) or (q14 and q13 and q12 and q11 and q10 and h9) or (q14 and q13 and q12 and q11 and q10 and q9 and h0) or (q14 and q13 and q12 and q11 and q10 and q9 and q8 and Cin));


S51 <= q0 xor Cin;

S52 <= q1 xor (h0 or (q0 and Cin));

S53 <= q2 xor (h1 or (q1 and h0) or (q1 and q0 and Cin));

S54 <= q3 xor (h2 or (q2 and h1) or (q2 and q1 and h0) or (q2 and q1 and q0 and Cin));

S55 <= q4 xor Cin;

S56 <= q5 xor (h4 or (q4 and Cin));
 
S57 <= q6 xor (h5 or (q5 and h4) or (q5 and q4 and Cin));

S58 <= q7 xor (h6 or (q6 and h5) or (q6 and q5 and h4) or (q6 and q5 and q4 and Cin));

S59 <= q8 xor Cin;

S60 <= q9 xor (h8 or (q8 and Cin));

S61 <= q10 xor (h9 or (q9 and h8) or (q9 and q8 and Cin));

S62 <= q11 xor (h10 or (q10 and h9) or (q10 and q9 and q8) or (q10 and q9 and q8 and Cin));

S63 <= q12 xor Cin;

S64 <= q13 xor (h12 or (q12 and Cin));

S65 <= q14 xor (h13 or (q13 and h12) or (q13 and q12 and Cin));

S66 <= q15 xor (h14 or (q14 and h13) or (q14 and q13 and q12) or (q14 and q13 and q12 and Cin));




S17 <= r0;

S18 <= r1;

S19 <= r2;

S20 <= r3;

S21 <= r4;

S22 <= r5;

S23 <= r6;

S24 <= r7;

S25 <= r8;

S26 <= r9;

S27 <= r10;

S28 <= r11;

S29 <= r12;

S30 <= r13;

S31 <= r14;

S32 <= r15;





END TypeArchitecture;
