// Logisim project AP6.circ as structural Verilog
module main (
  input  J,
  input  in_2,
  input  K,
  input  in_4,
  input  T,
  input  in_6,
  input  in_7,
  output out_8,
  output out_9,
  output out_10,
  output out_11
);

  wire clock_1_out, clock_2_out, n7404_1_pin2, n7404_1_pin12, n7424_1_pin4, n7424_1_pin5, n7424_1_pin6,
       n7424_2_pin1, n7424_2_pin2, n7424_2_pin3;

  _7404 #(.ShowInternalStructure("true")) u_7404_1 (
    .pin1(T), .pin2(n7404_1_pin2), .pin13(K), .pin12(n7404_1_pin12));  // open: pin3, pin4, pin5, pin6, pin11, pin10, pin9, pin8
  _7424 #(.ShowInternalStructure("true")) u_7424_1 (
    .pin4(n7424_1_pin4), .pin5(n7424_1_pin5), .pin6(n7424_1_pin6), .pin13(T), .pin12(out_11),
    .pin11(n7424_1_pin4), .pin10(n7404_1_pin2), .pin9(out_10), .pin8(n7424_1_pin5));  // open: pin1, pin2, pin3
  _7424 #(.ShowInternalStructure("true")) u_7424_2 (
    .pin1(n7424_2_pin1), .pin2(n7424_2_pin2), .pin3(n7424_2_pin3), .pin4(n7404_1_pin12), .pin5(out_8),
    .pin6(n7424_2_pin2), .pin13(J), .pin12(out_9), .pin11(n7424_2_pin1));  // open: pin10, pin9, pin8
  Clock clock_1 (.out(clock_1_out));
  Clock clock_2 (.out(clock_2_out));
  flipfloptd flipfloptd_1 (.D(n7424_2_pin3), .clock(clock_1_out), .set(in_2), .clear(in_4), .Q(out_8), .QN(out_9));
  flipfloptd flipfloptd_2 (.D(n7424_1_pin6), .clock(clock_2_out), .set(in_6), .clear(in_7), .Q(out_10), .QN(out_11));

  // Notes on the sheet:
  //   Flip-Flop JK
  //   Flip-Flop tipo T
endmodule

// VHDL entity flipfloptd, as the project stores it:
--------------------------------------------------------------------------------
-- Project :
-- File    :
-- Autor   :
-- Date    :
--
--------------------------------------------------------------------------------
-- Description :
--
--------------------------------------------------------------------------------

LIBRARY ieee;
USE ieee.std_logic_1164.all;

ENTITY flipfloptd IS
  PORT (
  ------------------------------------------------------------------------------
  --Insert input ports below
    D, clock, set, clear : IN std_logic;
    Q, QN : OUT std_logic
  ------------------------------------------------------------------------------
  --Insert output ports below
    
    );
END flipfloptd;

--------------------------------------------------------------------------------
--Complete your VHDL description below
--------------------------------------------------------------------------------

ARCHITECTURE TypeArchitecture OF flipfloptd IS

signal qi : std_logic;

BEGIN
procD: process(clock, set, clear)
	BEGIN
	if (set = '1') then qi <= '1';
	
	elsif (clear = '1') then qi <= '0';
	
	elsif rising_edge(clock) then
	qi <= D;
	end if;
	end process procD;
Q <= qi;
QN <= not qi;
END TypeArchitecture;
