// Logisim project AP7.circ as structural Verilog
module main (
  input  in_1,
  input  \Saída_programada ,
  input  in_3,
  input  in_4,
  input  in_5,
  input  in_6,
  input  in_7,
  input  in_8,
  input  [3:0] in_9,
  output out_10,
  output out_11,
  output out_12,
  output out_13,
  output [3:0] out_14
);

  wire clock_1_out, clock_2_out, d_ff_1_qn, d_ff_2_qn, d_ff_3_qn, d_ff_4_qn, n7485_1_pin3, n7485_1_pin5,
       transistor_1_out;

  Clock clock_1 (.out(clock_1_out));
  D_Flip_Flop d_ff_1 (
    .D(d_ff_1_qn), .clk(clock_1_out), .Q(out_13), .Qn(d_ff_1_qn), .reset(transistor_1_out));  // open: preset
  Clock clock_2 (.out(clock_2_out));
  D_Flip_Flop d_ff_2 (
    .D(d_ff_2_qn), .clk(d_ff_1_qn), .Q(out_12), .Qn(d_ff_2_qn), .reset(transistor_1_out));  // open: preset
  _7485 #(.ShowInternalStructure("true")) u_7485_1 (
    .pin1(in_1), .pin3(n7485_1_pin3), .pin4(n7485_1_pin3), .pin5(n7485_1_pin5), .pin15(out_10),
    .pin14(\Saída_programada ), .pin13(out_11), .pin12(out_12), .pin11(in_3), .pin10(out_13), .pin9(in_4));  // open: pin2, pin6, pin7
  D_Flip_Flop d_ff_3 (
    .D(d_ff_3_qn), .clk(d_ff_2_qn), .Q(out_11), .Qn(d_ff_3_qn), .reset(transistor_1_out));  // open: preset
  D_Flip_Flop d_ff_4 (
    .D(d_ff_4_qn), .clk(d_ff_3_qn), .Q(out_10), .Qn(d_ff_4_qn), .reset(transistor_1_out));  // open: preset
  Transistor transistor_1 (.in(n7485_1_pin5), .out(transistor_1_out), .gate(in_5));
  Contador contador_1 (
    .clock(clock_2_out), .areset_l_i(in_6), .en_h_i(in_7), .md_h_i(in_8), .numcfg(in_9), .cnt_o(out_14));
  // also tied to VCC on the sheet: n7485_1_pin3

  // Notes on the sheet:
  //   Module 0 - H
  //   Module 1 - L
  //   Saída do contador
endmodule

// VHDL entity Contador, as the project stores it:
--------------------------------------------------------------------------------
-- Project :
-- File    :
-- Autor   :
-- Date    :
--
--------------------------------------------------------------------------------
-- Description :
--
--------------------------------------------------------------------------------

LIBRARY ieee;
USE ieee.std_logic_1164.all;

ENTITY Contador IS
  PORT (
  ------------------------------------------------------------------------------
  --Insert input ports below
    clock,areset_l_i,en_h_i : IN std_logic;
    md_h_i : IN std_logic;
    numcfg : IN std_logic_vector(3 DOWNTO 0);
  
  ------------------------------------------------------------------------------
  --Insert output ports below
  	cnt_o : OUT std_logic_vector(3 DOWNTO 0)
    
    );
END Contador;

--------------------------------------------------------------------------------
--Complete your VHDL description below
--------------------------------------------------------------------------------

ARCHITECTURE TypeArchitecture OF Contador IS

signal dA, qA : std_logic;
signal dB, qB : std_logic;
signal dC, qC : std_logic;
signal dD, qD : std_logic;
signal A0, B0 : std_logic;
signal A1, B1 : std_logic;
signal A2, B2 : std_logic;
signal A3, B3 : std_logic;
signal aeqb : std_logic;


BEGIN
	process(clock,areset_l_i)
	begin 
		if(areset_l_i = '0') then
			qA <= '0';
			qB <= '0';
			qC <= '0';
			qD <= '0';
		elsif(rising_edge(clock)) then
			qA <= dA;
			qB <= dB;
			qC <= dC;
			qD <= dD;
		     if(md_h_i = '1') then
				A0 <= en_h_i xor qA;
				A1 <= qA xor qB;
				A2 <= (qA and qB) xor qC;
				A3 <= ((qA and qB) and qC) xor qD;
				B0 <= numcfg(0);
				B1 <= numcfg(1);
				B2 <= numcfg(2);
				B3 <= numcfg(3);
				if(aeqb = '1') then
					qA <= '0';
					qB <= '0';
					qC <= '0';
					qD <= '0';
				end if;
			end if;
		end if;
	end process;

dA <= en_h_i xor qA;
dB <= qA xor qB;
dC <= (qA and qB) xor qC;
dD <= ((qA and qB) and qC) xor qD;
aeqb <= not((A3 xor B3) or (A2 xor B2) or (A1 xor B1) or (A0 xor B0));
cnt_o <= qD&qC&qB&qA;



END TypeArchitecture;
