// Logisim project AP8.circ as structural Verilog
module main (
  input  LOAD,
  input  S,
  input  Carga,
  input  in_4,
  input  in_5,
  input  in_6,
  input  in_7,
  input  [2:0] in_8
);

  wire and_1_out, and_2_out, and_3_out, and_4_out, and_5_out, and_6_out, and_7_out, and_8_out, and_9_out,
       and_10_out, and_11_out, clock_1_out, clock_2_out, d2_1_a, d2_1_b, d2_1_c, d2_1_d, d2_1_e, d2_1_f,
       d2_1_g, d_ff_1_q, d_ff_1_qn, d_ff_2_q, d_ff_2_qn, d_ff_3_q, d_ff_3_qn, d_ff_4_q, d_ff_4_qn, d_ff_5_q,
       d_ff_5_qn, d_ff_6_q, d_ff_6_qn, decod7s_1_a, decod7s_1_b, decod7s_1_c, decod7s_1_d, decod7s_1_e,
       decod7s_1_f, decod7s_1_g, demultiplexer_1_out0, demultiplexer_1_out1, demultiplexer_2_out0,
       demultiplexer_2_out1, demultiplexer_3_out0, demultiplexer_3_out1, multiplexer_1_out,
       multiplexer_2_out, multiplexer_3_out, multiplexer_4_out, multiplexer_5_out, multiplexer_6_out,
       multiplexer_7_out, or_1_out, or_2_out, or_3_out;
  wire [2:0] maqes_1_saida;

  Clock clock_1 (.out(clock_1_out));
  Demultiplexer demultiplexer_1 (.out0(demultiplexer_1_out0), .out1(demultiplexer_1_out1), .in(clock_2_out), .sel(S));
  and and_1 (and_1_out, ~demultiplexer_1_out1, S);  // AND_Gate
  MaqEs maqes_1 (.clock(clock_1_out), .load(in_6), .primos_par(in_7), .carga(in_8), .saida(maqes_1_saida));
  D_Flip_Flop d_ff_1 (.D(d_ff_1_qn), .clk(multiplexer_1_out), .Q(d_ff_1_q), .Qn(d_ff_1_qn));  // open: preset, reset
  Multiplexer multiplexer_1 (.in0(demultiplexer_1_out0), .in1(and_1_out), .out(multiplexer_1_out), .sel(S));
  D_Flip_Flop d_ff_2 (.D(d_ff_2_qn), .clk(d_ff_1_qn), .Q(d_ff_2_q), .Qn(d_ff_2_qn));  // open: preset, reset
  and and_2 (and_2_out, d_ff_1_q, demultiplexer_2_out1);
  and and_3 (and_3_out, d_ff_1_q, demultiplexer_2_out1);
  and and_4 (and_4_out, d_ff_1_q, ~demultiplexer_3_out1);  // AND_Gate
  and and_5 (and_5_out, demultiplexer_2_out1, ~demultiplexer_3_out1);  // AND_Gate
  and and_6 (and_6_out, ~d_ff_1_q, ~demultiplexer_2_out1, demultiplexer_3_out1);  // AND_Gate
  and and_7 (and_7_out, d_ff_1_q, demultiplexer_3_out1);
  and and_8 (and_8_out, demultiplexer_2_out1, demultiplexer_3_out1);
  D_Flip_Flop d_ff_3 (.D(d_ff_3_qn), .clk(d_ff_2_qn), .Q(d_ff_3_q), .Qn(d_ff_3_qn));  // open: preset, reset
  Demultiplexer demultiplexer_2 (.out0(demultiplexer_2_out0), .out1(demultiplexer_2_out1), .in(d_ff_2_q), .sel(S));
  Demultiplexer demultiplexer_3 (.out0(demultiplexer_3_out0), .out1(demultiplexer_3_out1), .in(d_ff_3_q), .sel(S));
  decod7s decod7s_1 (
    .entradas(maqes_1_saida), .a(decod7s_1_a), .b(decod7s_1_b), .c(decod7s_1_c), .d(decod7s_1_d),
    .e(decod7s_1_e), .f(decod7s_1_f), .g(decod7s_1_g));
  or or_1 (or_1_out, demultiplexer_3_out1, and_2_out);
  or or_2 (or_2_out, and_3_out, and_4_out, and_5_out, and_6_out);
  or or_3 (or_3_out, and_7_out, and_8_out);
  _7_Segment_Display u_7_segment_display_1 (
    .g(decod7s_1_g), .f(decod7s_1_f), .a(decod7s_1_a), .b(decod7s_1_b), .e(decod7s_1_e), .d(decod7s_1_d),
    .c(decod7s_1_c));  // open: dp
  and and_9 (and_9_out, ~in_5, ~in_5);  // AND_Gate
  and and_10 (and_10_out, ~in_4, ~in_4);  // AND_Gate
  and and_11 (and_11_out, ~Carga, ~Carga);  // AND_Gate
  Multiplexer multiplexer_2 (.in0(1'b0), .in1(or_1_out), .out(multiplexer_2_out), .sel(S));
  Multiplexer multiplexer_3 (.in0(demultiplexer_2_out0), .in1(or_2_out), .out(multiplexer_3_out), .sel(S));
  Multiplexer multiplexer_4 (.in0(demultiplexer_3_out0), .in1(or_3_out), .out(multiplexer_4_out), .sel(S));
  D_Flip_Flop d_ff_4 (.D(d_ff_4_qn), .Q(d_ff_4_q), .Qn(d_ff_4_qn), .preset(in_5), .reset(and_9_out));  // open: clk
  Multiplexer multiplexer_5 (.in0(multiplexer_2_out), .in1(d_ff_4_q), .out(multiplexer_5_out), .sel(LOAD));
  Multiplexer multiplexer_6 (.in0(multiplexer_3_out), .in1(d_ff_5_q), .out(multiplexer_6_out), .sel(LOAD));
  Multiplexer multiplexer_7 (.in0(multiplexer_4_out), .in1(d_ff_6_q), .out(multiplexer_7_out), .sel(LOAD));
  D_Flip_Flop d_ff_5 (.D(d_ff_5_qn), .clk(d_ff_4_qn), .Q(d_ff_5_q), .Qn(d_ff_5_qn), .preset(in_4), .reset(and_10_out));
  D_Flip_Flop d_ff_6 (.D(d_ff_6_qn), .clk(d_ff_5_qn), .Q(d_ff_6_q), .Qn(d_ff_6_qn), .preset(Carga), .reset(and_11_out));
  d2 d2_1 (
    .D1(multiplexer_5_out), .C1(multiplexer_6_out), .B1(multiplexer_7_out), .A1(1'b0), .a(d2_1_a),
    .b(d2_1_b), .c(d2_1_c), .d(d2_1_d), .e(d2_1_e), .f(d2_1_f), .g(d2_1_g));
  Clock clock_2 (.out(clock_2_out));
  _7_Segment_Display u_7_segment_display_2 (
    .g(d2_1_g), .f(d2_1_f), .a(d2_1_a), .b(d2_1_b), .e(d2_1_e), .d(d2_1_d), .c(d2_1_c));  // open: dp

  // Notes on the sheet:
  //   PARES L
  //   PRIMOS H
endmodule

// VHDL entity d2, as the project stores it:
--------------------------------------------------------------------------------
-- Project :
-- File    :
-- Autor   :
-- Date    :
--
--------------------------------------------------------------------------------
-- Description :
--
--------------------------------------------------------------------------------

LIBRARY ieee;
USE ieee.std_logic_1164.all;

ENTITY d2 IS
  PORT (
  ------------------------------------------------------------------------------
  --Insert input ports below
    D1         : IN  std_logic;
    C1         : IN  std_logic;
    B1         : IN  std_logic;
    A1         : IN  std_logic;
  ------------------------------------------------------------------------------
  --Insert output ports below
    a          : OUT std_logic;
    b          : OUT std_logic;
    c          : OUT std_logic;
    d          : OUT std_logic;
    e          : OUT std_logic;
    f          : OUT std_logic;
    g          : OUT std_logic
    );
END d2;

--------------------------------------------------------------------------------
--Complete your VHDL description below
--------------------------------------------------------------------------------

ARCHITECTURE TypeArchitecture OF d2 IS

BEGIN

a <= (not A1 and not B1 and not C1 and not D1) or (not A1 and C1) or (not A1 and B1 and not C1 and D1) or (A1 and not C1 and not D1) or (A1 and not B1 and not C1) or (A1 and B1 and C1) or (A1 and C1 and not D1);
b <= (not A1 and not B1 and not C1) or (not A1 and not C1 and not D1) or (not A1 and not B1 and C1) or (not A1 and C1 and D1) or (A1 and not C1 and D1) or (A1 and not B1 and not D1) or (A1 and not B1 and C1 and not D1);
c <= (not A1 and not C1) or (not A1 and C1 and D1) or (not A1 and B1 and C1) or (A1 and not C1 and D1) or (A1 and not B1 and not C1) or (A1 and not B1 and C1);
d <= (not A1 and not B1 and not D1) or ( not A1 and not B1 and C1) or (B1 and C1 and not D1) or (B1 and not C1 and D1) or (A1 and not C1 and not D1) or (A1 and not B1 and C1 and D1);
e <= (not A1 and not B1 and not D1) or ( not A1 and C1 and not D1) or (A1 and C1) or (A1 and B1 and not C1) or (A1 and not B1 and not C1 and not D1);
f <= (A1 and C1) or (A1 and not B1 and not C1) or (A1 and not C1 and not D1) or (not A1 and B1 and not C1) or (not A1 and B1 and not D1) or (not A1 and not C1 and not D1);
g <= (A1 and C1) or (A1 and not B1 and not C1) or (A1 and not C1 and D1) or (not A1 and B1 and not C1) or (not A1 and not B1 and C1) or (not A1 and C1 and not D1);


END TypeArchitecture;

// VHDL entity MaqEs, as the project stores it:
--------------------------------------------------------------------------------
-- Project :
-- File    :
-- Autor   :
-- Date    :
--
--------------------------------------------------------------------------------
-- Description :
--
--------------------------------------------------------------------------------

LIBRARY ieee;
LIBRARY work;
USE ieee.std_logic_1164.all;

ENTITY MaqEs IS
  PORT (
  ------------------------------------------------------------------------------
  clock,load : IN std_logic;
  primos_par  : IN std_logic;
  carga : IN std_logic_vector(2 DOWNTO 0);
  saida : OUT std_logic_vector(2 DOWNTO 0)
  
  
    );
END MaqEs;

--------------------------------------------------------------------------------
--Complete your VHDL description below
--------------------------------------------------------------------------------

ARCHITECTURE TypeArchitecture OF MaqEs IS
type tipo_estado is (E0,E2,E3,E5,E7,F0,F2,F4,F6,G0);
signal estado, prox_estado : tipo_estado;
signal saida2 : std_logic_vector(2 DOWNTO 0);


BEGIN
mudaestado: process(clock,load)
begin
	 if load = '1' then 
	 	if carga = "000" then 
	 		saida <= "000";
	 	elsif carga = "001" then 
	 		saida <= "001";
	 	elsif carga = "010" then 
	 		saida <= "010";
	 	elsif carga = "011" then 
	 		saida <= "011";
	 	elsif carga = "100" then 
	 		saida <= "100";
	 	elsif carga = "101" then 
	 		saida <= "101";
	 	elsif carga = "110" then 
	 		saida <= "110";
	 	elsif carga = "111" then 
	 		saida <= "111";
	 	end if;
	 elsif rising_edge(clock) then 
	 		 saida <= saida2;
			 if primos_par = '1' then 
			    estado <= prox_estado;
			 else 
			    estado <= prox_estado;
			 end if;
	 end if;
end process;

 transicao: process(estado,primos_par)
 begin 
	 if primos_par = '1' then 
	 	case estado is 
	 	when E0 => prox_estado <= E2;
	 	when E2 => prox_estado <= E3;
	 	when E3 => prox_estado <= E5;
	 	when E5 => prox_estado <= E7;
	 	when E7 => prox_estado <= E0;
	 	when F0 => prox_estado <= E0;
	 	when F2 => prox_estado <= E0;
	 	when F4 => prox_estado <= E0;
	 	when F6 => prox_estado <= E0;
	 	when G0 => prox_estado <= E0;
	 	end case;
	 else 
	 	case estado is 
	 	when F0 => prox_estado <= F2;
	 	when F2 => prox_estado <= F4;
	 	when F4 => prox_estado <= F6;
	 	when F6 => prox_estado <= F0;
	 	when E0 => prox_estado <= F0;
	 	when E2 => prox_estado <= F0;
	 	when E3 => prox_estado <= F0;
	 	when E5 => prox_estado <= F0;
	 	when E7 => prox_estado <= F0;
	 	when G0 => prox_estado <= F0;
	 	end case;
	 end if;
 end process;


saidas: process(estado)
begin
	case estado is
	when E0 => saida2 <= "010";
	when E2 => saida2 <= "011";
	when E3 => saida2 <= "101";
	when E5 => saida2 <= "111";
	when E7 => saida2 <= "010";
	when F0 => saida2 <= "000";
	when F2 => saida2 <= "010";
	when F4 => saida2 <= "100";
	when F6 => saida2 <= "110";
	when G0 => saida2 <= "001";
	end case;
end process;



END TypeArchitecture;

// VHDL entity decod7s, as the project stores it:
--------------------------------------------------------------------------------
-- Project :
-- File    :
-- Autor   :
-- Date    :
--
--------------------------------------------------------------------------------
-- Description :
--
--------------------------------------------------------------------------------

LIBRARY ieee;
USE ieee.std_logic_1164.all;

entity decod7s is

    port
    (
       entradas : IN std_logic_vector(2 DOWNTO 0);
       a,b,c,d,e,f,g : OUT std_logic
    );
end decod7s;

architecture TypeArchitecture of decod7s is
    signal S : std_logic_vector(0 to 6);
begin
    with entradas select
        S <= "1111110" when "000", -- '0'
        "0110000" when "001", -- '1'
        "1101101" when "010", -- '2'
        "1111001" when "011", -- '3'
        "0110011" when "100", -- '4'
        "1011011" when "101", -- '5'
        "1011111" when "110", -- '6'
        "1110000" when "111", -- '7'
        "0000000" when others;

a <= S(0);
b <= S(1);
c <= S(2);
d <= S(3);
e <= S(4);
f <= S(5);
g <= S(6);

END TypeArchitecture;
