// Logisim project APF(Jogo21).circ as structural Verilog
module main (
  input  Parar,
  input  Reiniciar,
  output ONLINE
);

  wire decoder1_1_a, decoder1_1_b, decoder1_1_c, decoder1_1_d, decoder1_1_e, decoder1_1_f, decoder1_1_g,
       decoder1_2_a, decoder1_2_b, decoder1_2_c, decoder1_2_d, decoder1_2_e, decoder1_2_f, decoder1_2_g,
       decoder2_1_a, decoder2_1_b, decoder2_1_c, decoder2_1_d, decoder2_1_e, decoder2_1_f, decoder2_1_g,
       decoder2_2_a, decoder2_2_b, decoder2_2_c, decoder2_2_d, decoder2_2_e, decoder2_2_f, decoder2_2_g,
       decoder_dado_1_a, decoder_dado_1_b, decoder_dado_1_c, decoder_dado_1_d, decoder_dado_1_e,
       decoder_dado_1_f, decoder_dado_1_g, decoder_dado_2_a, decoder_dado_2_b, decoder_dado_2_c,
       decoder_dado_2_d, decoder_dado_2_e, decoder_dado_2_f, decoder_dado_2_g, decoder_dado_3_a,
       decoder_dado_3_b, decoder_dado_3_c, decoder_dado_3_d, decoder_dado_3_e, decoder_dado_3_f,
       decoder_dado_3_g, decoder_placar_1_a, decoder_placar_1_b, decoder_placar_1_c, decoder_placar_1_d,
       decoder_placar_1_e, decoder_placar_1_f, decoder_placar_1_g, decoder_placar_2_a, decoder_placar_2_b,
       decoder_placar_2_c, decoder_placar_2_d, decoder_placar_2_e, decoder_placar_2_f, decoder_placar_2_g,
       demultiplexer_1_out1, Girar_Dado_out, jogo21_1_cpu_w, jogo21_1_j1_w, or_1_out, Somar_J1_out;
  wire [4:0] jogo21_1_bot_sum, jogo21_1_dado_visor, jogo21_1_lstnum_cpu, jogo21_1_lstnum_j1,
       jogo21_1_somatotal;

  Clock Girar_Dado (.out(Girar_Dado_out));
  Button Somar_J1 (.out(Somar_J1_out));
  decoder_dado decoder_dado_1 (
    .entradas(jogo21_1_dado_visor), .a(decoder_dado_1_a), .b(decoder_dado_1_b), .c(decoder_dado_1_c),
    .d(decoder_dado_1_d), .e(decoder_dado_1_e), .f(decoder_dado_1_f), .g(decoder_dado_1_g));
  // AND_Gate and_1 has open pins: in0=demultiplexer_1_out1, out=open
  _7_Segment_Display u_7_segment_display_1 (
    .g(decoder_dado_1_g), .f(decoder_dado_1_f), .a(decoder_dado_1_a), .b(decoder_dado_1_b),
    .e(decoder_dado_1_e), .d(decoder_dado_1_d), .c(decoder_dado_1_c));  // open: dp
  JOGO21 jogo21_1 (
    .Dado(Girar_Dado_out), .Somar(Somar_J1_out), .CPU_turn(Parar), .Ajd(jogo21_1_bot_sum),
    .Bcd(jogo21_1_somatotal), .reset(demultiplexer_1_out1), .Dado_visor(jogo21_1_dado_visor),
    .SomaTotal(jogo21_1_somatotal), .LstNum_J1(jogo21_1_lstnum_j1), .Bot_sum(jogo21_1_bot_sum),
    .LstNum_CPU(jogo21_1_lstnum_cpu), .CPU_w(jogo21_1_cpu_w), .J1_W(jogo21_1_j1_w));
  LED led_1 (.in(jogo21_1_cpu_w));
  decoder_placar decoder_placar_1 (
    .entradas(jogo21_1_cpu_w), .a(decoder_placar_1_a), .b(decoder_placar_1_b), .c(decoder_placar_1_c),
    .d(decoder_placar_1_d), .e(decoder_placar_1_e), .f(decoder_placar_1_f), .g(decoder_placar_1_g));
  _7_Segment_Display u_7_segment_display_2 (
    .g(decoder_placar_1_g), .f(decoder_placar_1_f), .a(decoder_placar_1_a), .b(decoder_placar_1_b),
    .e(decoder_placar_1_e), .d(decoder_placar_1_d), .c(decoder_placar_1_c));  // open: dp
  _7_Segment_Display u_7_segment_display_3 (
    .g(decoder1_1_g), .f(decoder1_1_f), .a(decoder1_1_a), .b(decoder1_1_b), .e(decoder1_1_e),
    .d(decoder1_1_d), .c(decoder1_1_c));  // open: dp
  decoder1 decoder1_1 (
    .entradas(jogo21_1_bot_sum), .a(decoder1_1_a), .b(decoder1_1_b), .c(decoder1_1_c), .d(decoder1_1_d),
    .e(decoder1_1_e), .f(decoder1_1_f), .g(decoder1_1_g));
  _7_Segment_Display u_7_segment_display_4 (
    .g(decoder1_2_g), .f(decoder1_2_f), .a(decoder1_2_a), .b(decoder1_2_b), .e(decoder1_2_e),
    .d(decoder1_2_d), .c(decoder1_2_c));  // open: dp
  decoder1 decoder1_2 (
    .entradas(jogo21_1_somatotal), .a(decoder1_2_a), .b(decoder1_2_b), .c(decoder1_2_c), .d(decoder1_2_d),
    .e(decoder1_2_e), .f(decoder1_2_f), .g(decoder1_2_g));
  _7_Segment_Display u_7_segment_display_5 (
    .g(decoder2_1_g), .f(decoder2_1_f), .a(decoder2_1_a), .b(decoder2_1_b), .e(decoder2_1_e),
    .d(decoder2_1_d), .c(decoder2_1_c));  // open: dp
  _7_Segment_Display u_7_segment_display_6 (
    .g(decoder2_2_g), .f(decoder2_2_f), .a(decoder2_2_a), .b(decoder2_2_b), .e(decoder2_2_e),
    .d(decoder2_2_d), .c(decoder2_2_c));  // open: dp
  decoder2 decoder2_1 (
    .entradas(jogo21_1_bot_sum), .a(decoder2_1_a), .b(decoder2_1_b), .c(decoder2_1_c), .d(decoder2_1_d),
    .e(decoder2_1_e), .f(decoder2_1_f), .g(decoder2_1_g));
  LED led_2 (.in(jogo21_1_j1_w));
  decoder2 decoder2_2 (
    .entradas(jogo21_1_somatotal), .a(decoder2_2_a), .b(decoder2_2_b), .c(decoder2_2_c), .d(decoder2_2_d),
    .e(decoder2_2_e), .f(decoder2_2_f), .g(decoder2_2_g));
  decoder_placar decoder_placar_2 (
    .entradas(jogo21_1_j1_w), .a(decoder_placar_2_a), .b(decoder_placar_2_b), .c(decoder_placar_2_c),
    .d(decoder_placar_2_d), .e(decoder_placar_2_e), .f(decoder_placar_2_f), .g(decoder_placar_2_g));
  Demultiplexer demultiplexer_1 (.out0(ONLINE), .out1(demultiplexer_1_out1), .in(or_1_out), .sel(Reiniciar));
  _7_Segment_Display u_7_segment_display_7 (
    .g(decoder_placar_2_g), .f(decoder_placar_2_f), .a(decoder_placar_2_a), .b(decoder_placar_2_b),
    .e(decoder_placar_2_e), .d(decoder_placar_2_d), .c(decoder_placar_2_c));  // open: dp
  or or_1 (or_1_out, decoder_placar_1_c, decoder_placar_2_c);
  _7_Segment_Display u_7_segment_display_8 (
    .g(decoder_dado_2_g), .f(decoder_dado_2_f), .a(decoder_dado_2_a), .b(decoder_dado_2_b),
    .e(decoder_dado_2_e), .d(decoder_dado_2_d), .c(decoder_dado_2_c));  // open: dp
  _7_Segment_Display u_7_segment_display_9 (
    .g(decoder_dado_3_g), .f(decoder_dado_3_f), .a(decoder_dado_3_a), .b(decoder_dado_3_b),
    .e(decoder_dado_3_e), .d(decoder_dado_3_d), .c(decoder_dado_3_c));  // open: dp
  decoder_dado decoder_dado_2 (
    .entradas(jogo21_1_lstnum_cpu), .a(decoder_dado_2_a), .b(decoder_dado_2_b), .c(decoder_dado_2_c),
    .d(decoder_dado_2_d), .e(decoder_dado_2_e), .f(decoder_dado_2_f), .g(decoder_dado_2_g));
  decoder_dado decoder_dado_3 (
    .entradas(jogo21_1_lstnum_j1), .a(decoder_dado_3_a), .b(decoder_dado_3_b), .c(decoder_dado_3_c),
    .d(decoder_dado_3_d), .e(decoder_dado_3_e), .f(decoder_dado_3_f), .g(decoder_dado_3_g));

  // Notes on the sheet:
  //   Control + K - DADO !
  //   DADO
  //   CPU WINS
  //   CPU
  //   JOGADOR
  //   J1 WINS !
  //   Número Anterior CPU
  //   Número Anterior J1
endmodule

// VHDL entity JOGO21, as the project stores it:
--------------------------------------------------------------------------------
-- Project :
-- File    :
-- Autor   :
-- Date    :
--
--------------------------------------------------------------------------------
-- Description :
--
--------------------------------------------------------------------------------

LIBRARY ieee;
LIBRARY work;
USE ieee.std_logic_1164.all;

ENTITY JOGO21 IS
  PORT (
  ------------------------------------------------------------------------------
  ---J1-------------
  Dado,Somar : IN std_logic;
  Dado_visor : OUT std_logic_vector(4 DOWNTO 0);
  SomaTotal : OUT std_logic_vector(4 DOWNTO 0);
  LstNum_J1: OUT std_logic_vector(4 DOWNTO 0);

  --- Bot------------------
  CPU_turn : IN std_logic;
  Bot_sum: OUT std_logic_vector(4 DOWNTO 0);
  LstNum_CPU: OUT std_logic_vector(4 DOWNTO 0);
  ------------------

  ----Decisão---
  Ajd, Bcd : IN STD_LOGIC_VECTOR(4 DOWNTO 0); 
  reset: IN std_logic;
  CPU_w,J1_W: OUT STD_LOGIC
    

  
    );
END JOGO21;

--------------------------------------------------------------------------------
--Complete your VHDL description below
--------------------------------------------------------------------------------

ARCHITECTURE TypeArchitecture OF JOGO21 IS
-- Implementação do DADO --
type tipo_estado is (E1,E2,E3,E4,E5,E6);
signal estado, prox_estado : tipo_estado;
signal saida2 : std_logic_vector(4 DOWNTO 0);

type tipo_estado2 is (F1,F2,F3,F4,F5,F6);
signal estado2, prox_estado2 : tipo_estado2;
signal saida3 : std_logic_vector(4 DOWNTO 0);

--  Armazenadores e sinais para algumas saidas --
signal armazenador : std_logic_vector(4 DOWNTO 0);
signal armazenador2 : std_logic_vector(4 DOWNTO 0);
signal somando : std_logic_vector(4 DOWNTO 0);
signal conta2 : std_logic_vector(4 DOWNTO 0);

----Decisão
signal J1, CPU : STD_LOGIC;
----

-- Implementação do somador --
signal N1 : std_logic_vector(4 DOWNTO 0);
signal N2 : std_logic_vector(4 DOWNTO 0);
signal A : std_logic_vector(4 DOWNTO 0);
signal B : std_logic_vector(4 DOWNTO 0);
signal Cin : std_logic;
signal q0 : std_logic;
signal h0 : std_logic;
signal q1 : std_logic;
signal h1 : std_logic;
signal q2 : std_logic;
signal h2 : std_logic;
signal q3 : std_logic;
signal h3 : std_logic;
signal q4 : std_logic;
signal h4 : std_logic;
signal S : std_logic_vector(4 DOWNTO 0);


---------Somador do Bot -------------
signal N1b : std_logic_vector(4 DOWNTO 0);
signal N2b : std_logic_vector(4 DOWNTO 0);
signal C : std_logic_vector(4 DOWNTO 0);
signal D : std_logic_vector(4 DOWNTO 0);
signal Cin2 : std_logic;
signal p0 : std_logic;
signal g0 : std_logic;
signal p1 : std_logic;
signal g1 : std_logic;
signal p2 : std_logic;
signal g2 : std_logic;
signal p3 : std_logic;
signal g3 : std_logic;
signal p4 : std_logic;
signal g4 : std_logic;
signal T : std_logic_vector(4 DOWNTO 0);

signal bot_armazenador : std_logic_vector(4 DOWNTO 0);
signal bot_armazenador2 : std_logic_vector(4 DOWNTO 0);
signal bot_somando : std_logic_vector(4 DOWNTO 0);

-- Bot ------------------
signal  Dado2,an,sinal : std_logic;


-----sinal------

------------------
BEGIN
	Cin <= '0';
	
	
	h0 <= A(0) and B(0);
	q0 <= A(0) xor B(0);
	
	h1 <= A(1) and B(1);
	q1 <= A(1) xor B(1);
	
	h2 <= A(2) and B(2);
	q2 <= A(2) xor B(2);
	
	h3 <= A(3) and B(3);
	q3 <= A(3) xor B(3);
	
	h4 <= A(4) and B(4);
	q4 <= A(4) xor B(4);
	
	
	
	S(0) <= q0 xor Cin;
	
	S(1) <= q1 xor (h0 or (q0 and Cin));
	
	S(2) <= q2 xor (h1 or (q1 and h0) or (q1 and q0 and Cin));
	
	S(3) <= q3 xor (h2 or (q2 and h1) or (q2 and q1 and h0) or (q2 and q1 and q0 and Cin));
	
	S(4) <= q4 xor (h3 or (q3 and h2) or (q3 and q2 and h1) or (q3 and q2 and q1 and h0) or (q3 and q2 and q1 and q0 and Cin));
	
	--- Ainda o somador -- termina aqui!
	
	
	Cin2 <= '0';
	
	g0 <= C(0) and D(0);
	p0 <= C(0) xor D(0);
	
	g1 <= C(1) and D(1);
	p1 <= C(1) xor D(1);
	
	g2 <= C(2) and D(2);
	p2 <= C(2) xor D(2);
	
	g3 <= C(3) and D(3);
	p3 <= C(3) xor D(3);
	
	g4 <= C(4) and D(4);
	p4 <= C(4) xor D(4);
	
	
	
	T(0) <= p0 xor Cin2;
	
	T(1) <= p1 xor (g0 or (p0 and Cin2));
	
	T(2) <= p2 xor (g1 or (p1 and g0) or (p1 and p0 and Cin2));
	
	T(3) <= p3 xor (g2 or (p2 and g1) or (p2 and p1 and g0) or (p2 and p1 and p0 and Cin2));
	
	T(4) <= p4 xor (g3 or (p3 and g2) or (p3 and p2 and g1) or (p3 and p2 and p1 and g0) or (p3 and p2 and p1 and p0 and Cin2));
	---------------------------------------------------------------------------

	-- Aqui o dado foi implementado de maneira que funcionasse juntamente ao somador --
	-- Logo ele armazena as quantidades e soma com o resultado da soma -- 
	
	
	mudaestado: process(Dado,Somar,saida2,armazenador,reset,bot_armazenador)
	begin 
		
		 Dado_visor <= saida2;
		 N1 <= somando;
		 SomaTotal <= S;
		 LstNum_J1 <= armazenador;
		 --- Bot
		N1b <= bot_somando;
		Bot_sum <= T;
		LstNum_CPU <= bot_armazenador;

		if S > T then 
		for i in 0 to 5 loop
			if CPU_turn = '1'  then
				bot_armazenador <= saida3;
				bot_somando <= bot_armazenador;
				C <= bot_armazenador;
			 	if bot_somando = bot_armazenador then
			 		bot_armazenador2 <= saida3;
			 		N2b <= bot_armazenador2;
			 		D <= bot_armazenador2;
			 		if D > "00000" then 
			 			D <= T;
			 		end if;
			 	end if;
			 end if;
			if S < T then 
				exit;
			end if;
		end loop;
		end if;
	 	
		if reset = '1' then 
			SomaTotal <= "00000";
			Bot_sum <= "00000";
			A <= "00000";
			B <= "00000";
			C <= "00000";
			D <= "00000"; 
			somando <= "00000";
			LstNum_CPU <= "00000";
			LstNum_J1 <= "00000";
			bot_somando <= "00000";
		end if;
		
		 	
		if Somar = '1' then
		 	armazenador <= saida2;
		 	somando <= armazenador;
		 	A <= armazenador;
		 	if somando = armazenador then
		 		armazenador2 <= saida2;
		 		N2 <= armazenador2;
		 		B <= armazenador2;
		 		if B > "00000" then 
		 			B <= S;
		 		end if;
		 	end if;
		end if;
		if rising_edge(Dado) and Somar = '0' then 
				 estado <= prox_estado;
		------------------Bot ------------------
		end if;
		
		------------------------------------------
	end process;

	---- Decisão 
		
	J1 <= '1' WHEN Ajd < Bcd ELSE '0' ;
	CPU <= '1' WHEN Ajd > Bcd ELSE '0' ;

	---------
	process(S,T)
	begin
	if  T > "10101"  then 
		J1_w <= '1';
		CPU_w <= '0';
	elsif S > "10101" then 
		J1_w <= '0';
		CPU_w <= '1';
	elsif (S = "10101") then
		J1_w <= '1';
		CPU_w <= '0';
	elsif (T = "10101") then
		J1_w <= '0';
		CPU_w <= '1';
	elsif T > S then
		J1_w <= '0';
		CPU_w <= '1';
	end if;

	end process;

	
	 transicao: process(estado)
	 begin 
		 	case estado is 
		 	when E1 => prox_estado <= E2;
		 	when E2 => prox_estado <= E3;
		 	when E3 => prox_estado <= E4;
		 	when E4 => prox_estado <= E5;
		 	when E5 => prox_estado <= E6;
		 	when E6 => prox_estado <= E1;
		 	end case;
	 end process;
	
	
	saidas: process(estado)
	begin
		case estado is
		when E1 => saida2 <= "00001";
		when E2 => saida2 <= "00010";
		when E3 => saida2 <= "00011";
		when E4 => saida2 <= "00100";
		when E5 => saida2 <= "00101";
		when E6 => saida2 <= "00110";
		end case;
	end process;

	--- segundo contador --- 

	
	
	mudaestado2: process(Dado2,saida3)
	begin
	
	if rising_edge(Dado2) then 
			estado2 <= prox_estado2;
	end if; 
	end process;
	
				 
	 transicao2: process(estado2)
	 begin 
		 	case estado2 is 
		 	when F1 => prox_estado2 <= F2;
		 	when F2 => prox_estado2 <= F3;
		 	when F3 => prox_estado2 <= F4;
		 	when F4 => prox_estado2 <= F5;
		 	when F5 => prox_estado2 <= F6;
		 	when F6 => prox_estado2 <= F1;
		 	end case;
	 end process;
	
	
	saidas2: process(estado2)
	begin
		case estado2 is
		when F1 => saida3 <= "00001";
		when F2 => saida3 <= "00010";
		when F3 => saida3 <= "00011";
		when F4 => saida3 <= "00100";
		when F5 => saida3 <= "00101";
		when F6 => saida3 <= "00110";
		end case;
	end process;

	process
	begin
	an <= '1';
	wait for 100 ns;
	Dado2 <= '1';
	wait for 100 ns;
	Dado2 <= '0';
	wait for 100 ns;
	Dado2 <= '1';
	wait for 100 ns;
	an <= '0';
	end process;

	
END TypeArchitecture;

// VHDL entity decoder1, as the project stores it:
--------------------------------------------------------------------------------
-- Project :
-- File    :
-- Autor   :
-- Date    :
--
--------------------------------------------------------------------------------
-- Description :
-- FAZER UM DECODER COM 1-1, 1-2, 1-3
-- E OUTRO COM 2 DE 12, 3 DE 13...
--------------------------------------------------------------------------------

LIBRARY ieee;
USE ieee.std_logic_1164.all;

entity decoder1 is

    port
    (
       entradas : IN std_logic_vector(4 DOWNTO 0);
       a,b,c,d,e,f,g : OUT std_logic
    );
end decoder1;

architecture TypeArchitecture of decoder1 is
    signal S : std_logic_vector(0 to 6);
begin
    with entradas select
        S <= "1111110" when "00000", -- '0'
        "1111110" when "00001", -- '0'
        "1111110" when "00010", -- '0'
        "1111110" when "00011", -- '0'
        "1111110" when "00100", -- '0'
        "1111110" when "00101", -- '0'
        "1111110" when "00110", -- '0'
        "1111110" when "00111", -- '0'
        "1111110" when "01000", -- '0'
        "1111110" when "01001", -- '0'
        "0110000" when "01010", -- '1'
        "0110000" when "01011", -- '1'
        "0110000" when "01100", -- '1'
        "0110000" when "01101", -- '1'
        "0110000" when "01110", -- '1'
        "0110000" when "01111", -- '1'
        "0110000" when "10000", -- '1'
        "0110000" when "10001", -- '1'
        "0110000" when "10010", -- '1'
        "0110000" when "10011", -- '1'
        "1101101" when "10100", -- '2'
        "1101101" when "10101", -- '2'
        "1101101" when "10110", -- '2'
        "1101101" when "10111", -- '2'
        "1101101" when "11000", -- '2'
        "1101101" when "11001", -- '2'
        "1101101" when "11010", -- '2'
        
        "0000000" when others;

a <= S(0);
b <= S(1);
c <= S(2);
d <= S(3);
e <= S(4);
f <= S(5);
g <= S(6);

END TypeArchitecture;

// VHDL entity decoder2, as the project stores it:
--------------------------------------------------------------------------------
-- Project :
-- File    :
-- Autor   :
-- Date    :
--
--------------------------------------------------------------------------------
-- Description :
-- FAZER UM DECODER COM 1-1, 1-2, 1-3
-- E OUTRO COM 2 DE 12, 3 DE 13...
--------------------------------------------------------------------------------

LIBRARY ieee;
USE ieee.std_logic_1164.all;

entity decoder2 is

    port
    (
       entradas : IN std_logic_vector(4 DOWNTO 0);
       a,b,c,d,e,f,g : OUT std_logic
    );
end decoder2;

architecture TypeArchitecture of decoder2  is
    signal S : std_logic_vector(0 to 6);
begin
    with entradas select
        S <= "1111110" when "00000", -- '0'
        "0110000" when "00001", -- '1'
        "1101101" when "00010", -- '2'
        "1111001" when "00011", -- '3'
        "0110011" when "00100", -- '4'
        "1011011" when "00101", -- '5'
        "1011111" when "00110", -- '6'
        "1110000" when "00111", -- '7'
        "1111111" when "01000", -- '8'
        "1110011" when "01001", -- '9'
        "1111110" when "01010", -- '0'
        "0110000" when "01011", -- '1'
        "1101101" when "01100", -- '2'
        "1111001" when "01101", -- '3'
        "0110011" when "01110", -- '4'
        "1011011" when "01111", -- '5'
        "1011111" when "10000", -- '6'
        "1110000" when "10001", -- '7'
        "1111111" when "10010", -- '8'
        "1110011" when "10011", -- '9'
        "1111110" when "10100", -- '0'
        "0110000" when "10101", -- '1'
        "1101101" when "10110", -- '2'
        "1111001" when "10111", -- '3'
        "0110011" when "11000", -- '4'
        "1011011" when "11001", -- '5'
        "1011111" when "11010", -- '6'
        "XXXXXXX" when others;

a <= S(0);
b <= S(1);
c <= S(2);
d <= S(3);
e <= S(4);
f <= S(5);
g <= S(6);


END TypeArchitecture;

// VHDL entity decoder_dado, as the project stores it:
--------------------------------------------------------------------------------
-- Project :
-- File    :
-- Autor   :
-- Date    :
--
--------------------------------------------------------------------------------
-- Description :
-- FAZER UM DECODER COM 1-1, 1-2, 1-3
-- E OUTRO COM 2 DE 12, 3 DE 13...
--------------------------------------------------------------------------------

LIBRARY ieee;
USE ieee.std_logic_1164.all;

entity decoder_dado is

    port
    (
       entradas : IN std_logic_vector(4 DOWNTO 0);
       a,b,c,d,e,f,g : OUT std_logic
    );
end decoder_dado;

architecture TypeArchitecture of decoder_dado  is
    signal S : std_logic_vector(0 to 6);
begin
    with entradas select
        S <= "0110000" when "00001", -- '1'
        "1101101" when "00010", -- '2'
        "1111001" when "00011", -- '3'
        "0110011" when "00100", -- '4'
        "1011011" when "00101", -- '5'
        "1011111" when "00110", -- '6'
        "0000000" when others;

a <= S(0);
b <= S(1);
c <= S(2);
d <= S(3);
e <= S(4);
f <= S(5);
g <= S(6);

END TypeArchitecture;

// VHDL entity decisao, as the project stores it:
--------------------------------------------------------------------------------
-- Project :
-- File    :
-- Autor   :
-- Date    :
--
--------------------------------------------------------------------------------
-- Description :
--
--------------------------------------------------------------------------------

LIBRARY ieee;
USE ieee.std_logic_1164.all;

ENTITY decisao IS
  PORT (
    Ajd, Bcd: IN STD_LOGIC_VECTOR(4 DOWNTO 0) ;
    
    win  : IN STD_LOGIC;
    CPU_w,J1_W,draw : OUT STD_LOGIC
    
    

    );
END decisao;

--------------------------------------------------------------------------------
--Complete your VHDL description below
--------------------------------------------------------------------------------

ARCHITECTURE TypeArchitecture OF decisao IS
signal J1, CPU : STD_LOGIC;
begin
J1 <= '1' WHEN Ajd > Bcd ELSE '0' ;
CPU <= '1' WHEN Ajd < Bcd ELSE '0' ;

process(win)
begin
if win = '1' and J1 = '1' then 
	draw <= '0';
	J1_w <= '1';
	CPU_w <= '0';
elsif win = '1' and CPU = '1' then 
	draw <= '0';
	J1_w <= '0';
	CPU_w <= '1';
elsif win = '1' and CPU = '0' and J1 = '0' then
	draw <= '1';
	J1_w <= '0';
	CPU_w <= '0';
	
end if;
end process;
	


END TypeArchitecture;

// VHDL entity decoder_placar, as the project stores it:
--------------------------------------------------------------------------------
-- Project :
-- File    :
-- Autor   :
-- Date    :
--
--------------------------------------------------------------------------------
-- Description :
-- FAZER UM DECODER COM 1-1, 1-2, 1-3
-- E OUTRO COM 2 DE 12, 3 DE 13...
--------------------------------------------------------------------------------

LIBRARY ieee;
USE ieee.std_logic_1164.all;

entity decoder_placar is

    port
    (
       entradas : IN std_logic;
       a,b,c,d,e,f,g : OUT std_logic
    );
end decoder_placar;

architecture TypeArchitecture of decoder_placar  is
    signal S : std_logic_vector(0 to 6);
begin
    with entradas select
        S <= "1111110" when '0', -- '0'
        "0110000" when '1', -- '1'
        "0000000" when others;

a <= S(0);
b <= S(1);
c <= S(2);
d <= S(3);
e <= S(4);
f <= S(5);
g <= S(6);


END TypeArchitecture;

// VHDL entity decisao2, as the project stores it:
--------------------------------------------------------------------------------
-- Project :
-- File    :
-- Autor   :
-- Date    :
--
--------------------------------------------------------------------------------
-- Description :
--
--------------------------------------------------------------------------------

LIBRARY ieee;
USE ieee.std_logic_1164.all;

ENTITY decisao2 IS
  PORT (
    Ajd, Bcd: IN STD_LOGIC_VECTOR(4 DOWNTO 0) ;
   
    sinal : OUT STD_LOGIC
    
    

    );
END decisao2;

--------------------------------------------------------------------------------
--Complete your VHDL description below
--------------------------------------------------------------------------------

ARCHITECTURE TypeArchitecture OF decisao2 IS

signal J1, CPU : STD_LOGIC;
begin

J1 <= '1' WHEN Ajd > Bcd ELSE '0' ;
CPU <= '1' WHEN Ajd < Bcd ELSE '0' ;

process
begin
if CPU = '1' and J1 = '1' then 
	sinal <= '1';

end if;
end process;
	


END TypeArchitecture;
